// Logisim project lutcomp.circ as structural Verilog: 4 circuits, main circuit main
// 10
module main (
  output halt
);

  wire and_1_out, clock_1_out, comparator_1_gt, decoder_1_out0, decoder_1_out1, decoder_1_out2,
       decoder_1_out3, decoder_1_out4, decoder_2_out0, decoder_2_out1, decoder_2_out2, decoder_2_out3,
       decoder_3_out0, decoder_3_out1, decoder_3_out2, decoder_3_out3, key_ctrl_1_key_clk,
       key_ctrl_1_key_read_en, key_ctrl_1_rdy, keyboard_1_avail, mmu_1_key_discard, mmu_1_ttyclk, or_1_out,
       or_2_out;
  wire [1:0] undriven, undriven_2;
  wire [2:0] counter_1_q;
  wire [3:0] undriven_3, undriven_4;
  wire [4:0] rom_1_data;
  wire [6:0] keyboard_1_data, mmu_1_ttydata;
  wire [7:0] adder_1_out, lut_out_q, mmu_1_data_out, multiplexer_1_out, PC_q, register_1_q, rom_2_data, X_q;
  wire [7:4] controlled_buffer_2_out;
  wire [18:4] controlled_buffer_1_out;
  wire [23:0] ADDR_q;

  Clock clock_1 (.out(clock_1_out));
  Counter #(.width(3), .max('h4), .behavior("old")) counter_1 (
    .Q(counter_1_q), .clk(clock_1_out), .clr(halt));  // open: load, D, count, carry, preset
  Adder adder_1 (.a(PC_q), .b(8'h1), .out(adder_1_out));  // open: cin, cout
  Decoder #(.select(3), .disabled(0)) decoder_1 (
    .out0(decoder_1_out0), .out1(decoder_1_out1), .out2(decoder_1_out2), .out3(decoder_1_out3),
    .out4(decoder_1_out4), .sel(counter_1_q), .en(comparator_1_gt));  // open: out5, out6, out7
  Multiplexer #(.width(8), .enable("false")) multiplexer_1 (
    .in0(adder_1_out), .in1(lut_out_q), .out(multiplexer_1_out), .sel(decoder_3_out2));
  Register #(.Select("low")) register_1 (
    .D(multiplexer_1_out), .Q(register_1_q), .clk(decoder_1_out3));  // open: en, clr
  Register #(.Select("low")) PC (.D(register_1_q), .Q(PC_q), .clk(decoder_1_out4));  // open: en, clr
  Register #(.Select("low")) X (.D(lut_out_q), .en(decoder_3_out0), .Q(X_q), .clk(decoder_1_out3));  // open: clr
  // Probe on undriven
  Comparator comparator_1 (.a(PC_q), .b({8{1'b1}}), .gt(comparator_1_gt), .eq(halt));  // open: lt
  // Probe on rom_1_data[3:0]
  ROM #(.Select("high")) rom_1 (.addr(PC_q), .data({controlled_buffer_1_out[14:12], rom_1_data}));
  // Probe on undriven_2
  Register #(.Select("low")) ADDR (
    .D(lut_out_q), .en(decoder_3_out1), .Q(ADDR_q[7:0]), .clk(decoder_1_out3));  // open: clr
  Keyboard keyboard_1 (
    .clk(key_ctrl_1_key_clk), .re(key_ctrl_1_key_read_en), .avail(keyboard_1_avail), .data(keyboard_1_data));  // open: clr
  assign controlled_buffer_1_out[7:4] = decoder_2_out0 ? rom_1_data[3:0] : 4'bz;  // Controlled_Buffer controlled_buffer_1
  Decoder #(.select(2), .disabled(0), .enable("false")) decoder_2 (
    .out0(decoder_2_out0), .out1(decoder_2_out1), .out2(decoder_2_out2), .out3(decoder_2_out3), .sel(undriven));
  key_ctrl key_ctrl_1 (
    .key_avail(keyboard_1_avail), .discard(mmu_1_key_discard), .key_clk(key_ctrl_1_key_clk),
    .key_read_en(key_ctrl_1_key_read_en), .rdy(key_ctrl_1_rdy));
  // Probe on controlled_buffer_1_out[14:12]
  assign {controlled_buffer_2_out, controlled_buffer_1_out[7:4]} = decoder_2_out1 ? ADDR_q[7:0] : 8'bz;  // Controlled_Buffer controlled_buffer_2
  assign {controlled_buffer_2_out, controlled_buffer_1_out[7:4]} = decoder_2_out2 ? PC_q : 8'bz;  // Controlled_Buffer controlled_buffer_3
  assign {controlled_buffer_2_out, controlled_buffer_1_out[7:4]} = decoder_2_out3 ? mmu_1_data_out : 8'bz;  // Controlled_Buffer controlled_buffer_4
  mmu mmu_1 (
    .data_in(lut_out_q), .key_char(keyboard_1_data), .key_rdy(key_ctrl_1_rdy), .addr(ADDR_q),
    .store(and_1_out), .clk(or_1_out), .key_discard(mmu_1_key_discard), .ttydata(mmu_1_ttydata),
    .ttyclk(mmu_1_ttyclk), .data_out(mmu_1_data_out));
  // Probe on mmu_1_data_out
  TTY #(.trigger("falling")) tty_1 (.data(mmu_1_ttydata), .clk(mmu_1_ttyclk));  // open: we, clr
  // Probe on {controlled_buffer_2_out, controlled_buffer_1_out[7:4]}
  and and_1 (and_1_out, or_2_out, decoder_3_out3);
  or or_1 (or_1_out, decoder_1_out3, decoder_1_out1);
  or or_2 (or_2_out, decoder_1_out2, decoder_1_out3);
  // Probe on X_q
  Decoder #(.select(2), .disabled(0), .enable("false")) decoder_3 (
    .out0(decoder_3_out0), .out1(decoder_3_out1), .out2(decoder_3_out2), .out3(decoder_3_out3),
    .sel(undriven_2));
  ROM #(.addrWidth(19), .Select("high")) rom_2 (
    .addr({controlled_buffer_1_out[18:12], undriven_4, controlled_buffer_1_out[7:4], undriven_3}),
    .data(rom_2_data));
  Register #(.Select("low")) lut_out (.D(rom_2_data), .Q(lut_out_q), .clk(decoder_1_out1));  // open: en, clr
  // Pins of 4 and 8 bits meet at {controlled_buffer_2_out, controlled_buffer_1_out[7:4]}
  // Pins of 8 and 24 bits meet at ADDR_q
  // Pins of 15 and 19 bits meet at {controlled_buffer_1_out[18:12], undriven_4, controlled_buffer_1_out[7:4], undriven_3}

  // Notes on the sheet:
  //   instructions
  //   input sel
  //   out sel
  //   inst part2
  //   contents of rom_1 (hex, n*v repeats v):
  //   1 3e 0 ff 80 f9 1 ff 2 ff ff 7f 1 0 2e 1 1 1 ff 2 ff
  //   opcode
  //   operand2
  //   mem_data_out
  //   operand1/acc
  //   ALU LUT
  //   contents of rom_2 (hex, n*v repeats v):
  //   256*0 256*1 256*2 256*3 256*4 256*5 256*6 256*7 256*8 256*9 256*a 256*b 256*c 256*d 256*e 256*f
  //   256*10 256*11 256*12 256*13 256*14 256*15 256*16 256*17 256*18 256*19 256*1a 256*1b 256*1c 256*1d
  //   256*1e 256*1f 256*20 256*21 256*22 256*23 256*24 256*25 256*26 256*27 256*28 256*29 256*2a 256*2b
  //   256*2c 256*2d 256*2e 256*2f 256*30 256*31 256*32 256*33 256*34 256*35 256*36 256*37 256*38 256*39
  //   256*3a 256*3b 256*3c 256*3d 256*3e 256*3f 256*40 256*41 256*42 256*43 256*44 256*45 256*46 256*47
  //   256*48 256*49 256*4a 256*4b 256*4c 256*4d 256*4e 256*4f 256*50 256*51 256*52 256*53 256*54 256*55
  //   256*56 256*57 256*58 256*59 256*5a 256*5b 256*5c 256*5d 256*5e 256*5f 256*60 256*61 256*62 256*63
  //   256*64 256*65 256*66 256*67 256*68 256*69 256*6a 256*6b 256*6c 256*6d 256*6e 256*6f 256*70 256*71
  //   256*72 256*73 256*74 256*75 256*76 256*77 256*78 256*79 256*7a 256*7b 256*7c 256*7d 256*7e 256*7f
  //   256*80 256*81 256*82 256*83 256*84 256*85 256*86 256*87 256*88 256*89 256*8a 256*8b 256*8c 256*8d
  //   256*8e 256*8f 256*90 256*91 256*92 256*93 256*94 256*95 256*96 256*97 256*98 256*99 256*9a 256*9b
  //   256*9c 256*9d 256*9e 256*9f 256*a0 256*a1 256*a2 256*a3 256*a4 256*a5 256*a6 256*a7 256*a8 256*a9
  //   256*aa 256*ab 256*ac 256*ad 256*ae 256*af 256*b0 256*b1 256*b2 256*b3 256*b4 256*b5 256*b6 256*b7
  //   256*b8 256*b9 256*ba 256*bb 256*bc 256*bd 256*be 256*bf 256*c0 256*c1 256*c2 256*c3 256*c4 256*c5
  //   256*c6 256*c7 256*c8 256*c9 256*ca 256*cb 256*cc 256*cd 256*ce 256*cf 256*d0 256*d1 256*d2 256*d3
  //   256*d4 256*d5 256*d6 256*d7 256*d8 256*d9 256*da 256*db 256*dc 256*dd 256*de 256*df 256*e0 256*e1
  //   256*e2 256*e3 256*e4 256*e5 256*e6 256*e7 256*e8 256*e9 256*ea 256*eb 256*ec 256*ed 256*ee 256*ef
  //   256*f0 256*f1 256*f2 256*f3 256*f4 256*f5 256*f6 256*f7 256*f8 256*f9 256*fa 256*fb 256*fc 256*fd
  //   256*fe 256*ff 0 1 2 3 4 5 6 7 8 9 a b c d e f 10 11 12 13 14 15 16 17 18 19 1a 1b 1c 1d 1e 1f 20 21
  //   22 23 24 25 26 27 28 29 2a 2b 2c 2d 2e 2f 30 31 32 33 34 35 36 37 38 39 3a 3b 3c 3d 3e 3f 40 41 42
  //   43 44 45 46 47 48 49 4a 4b 4c 4d 4e 4f 50 51 52 53 54 55 56 57 58 59 5a 5b 5c 5d 5e 5f 60 61 62 63
  //   64 65 66 67 68 69 6a 6b 6c 6d 6e 6f 70 71 72 73 74 75 76 77 78 79 7a 7b 7c 7d 7e 7f 80 81 82 83 84
  //   85 86 87 88 89 8a 8b 8c 8d 8e 8f 90 91 92 93 94 95 96 97 98 99 9a 9b 9c 9d 9e 9f a0 a1 a2 a3 a4 a5
  //   a6 a7 a8 a9 aa ab ac ad ae af b0 b1 b2 b3 b4 b5 b6 b7 b8 b9 ba bb bc bd be bf c0 c1 c2 c3 c4 c5 c6
  //   c7 c8 c9 ca cb cc cd ce cf d0 d1 d2 d3 d4 d5 d6 d7 d8 d9 da db dc dd de df e0 e1 e2 e3 e4 e5 e6 e7
  //   e8 e9 ea eb ec ed ee ef f0 f1 f2 f3 f4 f5 f6 f7 f8 f9 fa fb fc fd fe ff 1 1 3 3 5 5 7 7 9 9 b b d d
  //   f f 11 11 13 13 15 15 17 17 19 19 1b 1b 1d 1d 1f 1f 21 21 23 23 25 25 27 27 29 29 2b 2b 2d 2d 2f 2f
  //   31 31 33 33 35 35 37 37 39 39 3b 3b 3d 3d 3f 3f 41 41 43 43 45 45 47 47 49 49 4b 4b 4d 4d 4f 4f 51
  //   51 53 53 55 55 57 57 59 59 5b 5b 5d 5d 5f 5f 61 61 63 63 65 65 67 67 69 69 6b 6b 6d 6d 6f 6f 71 71
  //   73 73 75 75 77 77 79 79 7b 7b 7d 7d 7f 7f 81 81 83 83 85 85 87 87 89 89 8b 8b 8d 8d 8f 8f 91 91 93
  //   93 95 95 97 97 99 99 9b 9b 9d 9d 9f 9f a1 a1 a3 a3 a5 a5 a7 a7 a9 a9 ab ab ad ad af af b1 b1 b3 b3
  //   b5 b5 b7 b7 b9 b9 bb bb bd bd bf bf c1 c1 c3 c3 c5 c5 c7 c7 c9 c9 cb cb cd cd cf cf d1 d1 d3 d3 d5
  //   d5 d7 d7 d9 d9 db db dd dd df df e1 e1 e3 e3 e5 e5 e7 e7 e9 e9 eb eb ed ed ef ef f1 f1 f3 f3 f5 f5
  //   f7 f7 f9 f9 fb fb fd fd ff ff 2 3 2 3 6 7 6 7 a b a b e f e f 12 13 12 13 16 17 16 17 1a 1b 1a 1b 1e
  //   1f 1e 1f 22 23 22 23 26 27 26 27 2a 2b 2a 2b 2e 2f 2e 2f 32 33 32 33 36 37 36 37 3a 3b 3a 3b 3e 3f
  //   3e 3f 42 43 42 43 46 47 46 47 4a 4b 4a 4b 4e 4f 4e 4f 52 53 52 53 56 57 56 57 5a 5b 5a 5b 5e 5f 5e
  //   5f 62 63 62 63 66 67 66 67 6a 6b 6a 6b 6e 6f 6e 6f 72 73 72 73 76 77 76 77 7a 7b 7a 7b 7e 7f 7e 7f
  //   82 83 82 83 86 87 86 87 8a 8b 8a 8b 8e 8f 8e 8f 92 93 92 93 96 97 96 97 9a 9b 9a 9b 9e 9f 9e 9f a2
  //   a3 a2 a3 a6 a7 a6 a7 aa ab aa ab ae af ae af b2 b3 b2 b3 b6 b7 b6 b7 ba bb ba bb be bf be bf c2 c3
  //   c2 c3 c6 c7 c6 c7 ca cb ca cb ce cf ce cf d2 d3 d2 d3 d6 d7 d6 d7 da db da db de df de df e2 e3 e2
  //   e3 e6 e7 e6 e7 ea eb ea eb ee ef ee ef f2 f3 f2 f3 f6 f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
endmodule

module mmu (
  input  [7:0] data_in,
  input  [6:0] key_char,
  input  key_rdy,
  input  [23:0] addr,
  input  store,
  input  clk,
  output key_discard,
  output [6:0] ttydata,
  output ttyclk,
  output [7:0] data_out
);

  wire and_1_out, and_2_out, and_3_out, comparator_1_eq, comparator_1_gt, comparator_1_lt, not_1_out;
  wire [7:0] controlled_buffer_4_out;

  assign data_out = store ? data_in : 8'bz;  // Controlled_Buffer controlled_buffer_1
  Comparator #(.width(24)) comparator_1 (
    .a(24'h1), .b(addr), .gt(comparator_1_gt), .eq(comparator_1_eq), .lt(comparator_1_lt));
  not not_1 (not_1_out, store);
  assign data_out = and_1_out ? {key_rdy, key_char} : 8'bz;  // Controlled_Buffer controlled_buffer_2
  and and_1 (and_1_out, comparator_1_gt, not_1_out);
  assign data_out = and_2_out ? 8'hcc : 8'bz;  // Controlled_Buffer controlled_buffer_3
  and and_2 (and_2_out, comparator_1_eq, not_1_out);
  assign controlled_buffer_4_out = store ? data_out : 8'bz;  // Controlled_Buffer controlled_buffer_4
  RAM #(.addrWidth(24), .Select("high")) ram_1 (
    .addr(addr), .data(controlled_buffer_4_out), .clk(clk), .ld(not_1_out));  // open: sel, clr
  assign data_out = and_3_out ? controlled_buffer_4_out : 8'bz;  // Controlled_Buffer controlled_buffer_5
  and and_3 (and_3_out, comparator_1_lt, not_1_out);
  and and_4 (key_discard, data_out[7], store, clk, comparator_1_gt);
  and and_5 (ttyclk, comparator_1_eq, store, clk);

  assign ttydata = data_out[6:0];

  // Notes on the sheet:
  //   addr == 1
  //   addr > 1
  //   addr == 0
endmodule

module key_ctrl (
  input  key_avail,
  input  discard,
  output key_clk,
  output key_read_en,
  output rdy
);

  wire and_1_out, and_3_out, and_4_out, clock_1_out, d_ff_1_q, d_ff_2_q, decoder_1_out0, decoder_1_out1,
       decoder_1_out2, decoder_1_out3, decoder_1_out4;
  wire [2:0] counter_1_q;

  Clock clock_1 (.out(clock_1_out));
  Decoder #(.select(3), .disabled(0), .enable("false")) decoder_1 (
    .out0(decoder_1_out0), .out1(decoder_1_out1), .out2(decoder_1_out2), .out3(decoder_1_out3),
    .out4(decoder_1_out4), .sel(counter_1_q));  // open: out5, out6, out7
  Counter #(.width(3), .max('h4), .trigger("falling"), .behavior("old")) counter_1 (
    .Q(counter_1_q), .clk(clock_1_out));  // open: load, D, count, carry, clr, preset
  or or_1 (key_clk, decoder_1_out0, and_1_out);
  and and_1 (and_1_out, decoder_1_out2, d_ff_2_q);
  or or_2 (key_read_en, decoder_1_out1, decoder_1_out2);
  D_Flip_Flop d_ff_1 (.clk(and_1_out), .D(1'b1), .Q(d_ff_1_q), .reset(and_4_out));  // open: Qn, preset
  D_Flip_Flop d_ff_2 (.clk(discard), .D(1'b1), .Q(d_ff_2_q), .reset(and_4_out));  // open: Qn, preset
  and and_2 (rdy, key_avail, ~and_3_out);  // AND_Gate
  and and_3 (and_3_out, d_ff_1_q, decoder_1_out3);
  and and_4 (and_4_out, d_ff_1_q, decoder_1_out4);
endmodule

module regs (
);

  wire decoder_1_out0, decoder_1_out1, undriven_2;
  wire [3:0] undriven, undriven_3;

  Decoder #(.select(4), .disabled(0), .enable("false")) decoder_1 (
    .out0(decoder_1_out0), .out1(decoder_1_out1));  // open: out2, out3, out4, out5, out6, out7, out8, out9, out10, out11, out12, out13, out14, out15, sel
  Register #(.width(4), .Select("low")) register_1 (
    .D(undriven), .en(decoder_1_out0), .clk(undriven_2));  // open: Q, clr
  Register #(.width(4), .Select("low")) register_2 (
    .D(undriven), .en(decoder_1_out1), .clk(undriven_2));  // open: Q, clr
  Register #(.width(4), .Select("low")) register_3 (.D(undriven));  // open: en, Q, clk, clr
  Register #(.width(4), .Select("low")) register_4 ();  // open: D, en, Q, clk, clr
  Register #(.width(4), .Select("low")) register_5 ();  // open: D, en, Q, clk, clr
  Register #(.width(4), .Select("low")) register_6 (.clk(undriven_3[0]));  // open: D, en, Q, clr
  Register #(.width(4), .Select("low")) register_7 (.D(undriven_3));  // open: en, Q, clk, clr
  Register #(.width(4), .Select("low")) register_8 ();  // open: D, en, Q, clk, clr
  // Pins of 1 and 4 bits meet at undriven_3
endmodule
