// Logisim project lutcomp.circ as structural Verilog: 11 circuits, main circuit main
// 10
module main (
  input  RESET,
  output halt
);

  wire and_1_out, and_2_out, clock_1_out, decoder_1_out0, decoder_1_out1, decoder_1_out2, decoder_2_out0,
       decoder_2_out1, decoder_2_out2, decoder_2_out3, decoder_2_out4, decoder_2_out5, decoder_2_out6,
       decoder_2_out7, decoder_2_out8, decoder_2_out9, decoder_2_out10, decoder_2_out11, decoder_2_out12,
       decoder_2_out13, decoder_2_out14, decoder_2_out15, decoder_3_out0, decoder_3_out1, decoder_3_out2,
       decoder_3_out3, decoder_3_out4, decoder_3_out5, decoder_3_out6, decoder_3_out7, decoder_3_out8,
       decoder_3_out9, decoder_3_out10, decoder_3_out11, decoder_3_out12, decoder_3_out13, decoder_3_out14,
       decoder_3_out15, key_ctrl_1_key_clk, key_ctrl_1_key_read_en, keyboard_1_avail, not_1_out, not_2_out,
       not_4_out, not_6_out, not_7_out, not_8_out, not_9_out, not_10_out, not_11_out, not_12_out, not_13_out,
       not_14_out, not_20_out, not_21_out, or_1_out, PC0_nrco;
  wire [6:0] keyboard_1_data;
  wire [7:0] A_zpeek, ADDR_q, ALU_LUT_data, B_zpeek, C_zpeek, controlled_buffer_1_out, IN1_q, IRH_q,
       IRL_zpeek, PC0_io_2, PC0_peek, ROM_data, TMP_zpeek, uIR_q, uLO_q, uPC_io_2, uROM_data;
  wire [7:7] key_ctrl_1_rdy;

  Clock clock_1 (.out(clock_1_out));
  not not_1 (not_1_out, RESET);
  and and_1 (and_1_out, PC0_nrco, clock_1_out);
  not not_2 (not_2_out, and_1_out);
  _74LS593 uPC (
    .IO(uPC_io_2), .IO_2(uPC_io_2), .nCCLR(and_2_out), .CCK(not_2_out));  // open: peek, nRCO, nCLOAD, nRCKEN, RCK, G, nG, CCKEN, nCCKEN
  and and_2 (and_2_out, not_1_out, ~decoder_3_out15);  // AND_Gate
  _74LS593 PC0 (
    .peek(PC0_peek), .nRCO(PC0_nrco), .IO(PC0_io_2), .nCLOAD(not_9_out), .nRCKEN(1'b0), .RCK(decoder_3_out5),
    .IO_2(PC0_io_2), .G(1'b0), .nG(not_10_out), .nCCLR(not_1_out), .nCCKEN(1'b0), .CCK(decoder_3_out12));  // open: CCKEN
  not not_3 (halt, PC0_nrco);
  // Probe on PC0_peek
  _74HCT374 uLO (.D(PC0_io_2), .CP(decoder_3_out11), .nOE(1'b0), .Q(uLO_q));  // open: Zpeek
  // Probe on uPC_io_2[1:0]
  // Probe on uPC_io_2[7:2]
  // Probe on uLO_q
  // Probe on IRH_q[2:0]
  // Probe on IRH_q[4:3]
  Decoder #(.select(2), .disabled(0)) decoder_1 (
    .out0(decoder_1_out0), .out1(decoder_1_out1), .out2(decoder_1_out2), .sel(uPC_io_2[1:0]), .en(and_1_out));  // open: out3
  // Probe on ROM_data
  ROM #(.Select("high")) ROM (.addr(PC0_io_2), .data(ROM_data));
  ROM #(.addrWidth(19), .Select("high")) uROM (.addr({IRH_q[4:0], uLO_q, uPC_io_2[7:2]}), .data(uROM_data));
  or or_1 (or_1_out, decoder_1_out0, decoder_1_out2);
  _74HCT374 uIR (.D(uROM_data), .CP(or_1_out), .nOE(1'b0), .Q(uIR_q));  // open: Zpeek
  not not_4 (not_4_out, decoder_2_out0);
  // NOT_Gate not_5 has open pins: in=decoder_2_out1, out=open
  not not_6 (not_6_out, decoder_2_out2);
  not not_7 (not_7_out, decoder_2_out3);
  not not_8 (not_8_out, decoder_2_out4);
  not not_9 (not_9_out, decoder_2_out5);
  not not_10 (not_10_out, decoder_2_out6);
  not not_11 (not_11_out, decoder_2_out7);
  not not_12 (not_12_out, decoder_2_out8);
  not not_13 (not_13_out, decoder_2_out9);
  not not_14 (not_14_out, decoder_2_out10);
  // NOT_Gate not_15 has open pins: in=decoder_2_out11, out=open
  // NOT_Gate not_16 has open pins: in=decoder_2_out12, out=open
  // NOT_Gate not_17 has open pins: in=decoder_2_out13, out=open
  // NOT_Gate not_18 has open pins: in=decoder_2_out14, out=open
  // NOT_Gate not_19 has open pins: in=decoder_2_out15, out=open
  Decoder #(.select(4), .disabled(0), .enable("false")) decoder_2 (
    .out0(decoder_2_out0), .out1(decoder_2_out1), .out2(decoder_2_out2), .out3(decoder_2_out3),
    .out4(decoder_2_out4), .out5(decoder_2_out5), .out6(decoder_2_out6), .out7(decoder_2_out7),
    .out8(decoder_2_out8), .out9(decoder_2_out9), .out10(decoder_2_out10), .out11(decoder_2_out11),
    .out12(decoder_2_out12), .out13(decoder_2_out13), .out14(decoder_2_out14), .out15(decoder_2_out15),
    .sel(uIR_q[7:4]));
  Decoder #(.select(4), .disabled(0)) decoder_3 (
    .out0(decoder_3_out0), .out1(decoder_3_out1), .out2(decoder_3_out2), .out3(decoder_3_out3),
    .out4(decoder_3_out4), .out5(decoder_3_out5), .out6(decoder_3_out6), .out7(decoder_3_out7),
    .out8(decoder_3_out8), .out9(decoder_3_out9), .out10(decoder_3_out10), .out11(decoder_3_out11),
    .out12(decoder_3_out12), .out13(decoder_3_out13), .out14(decoder_3_out14), .out15(decoder_3_out15),
    .sel(uIR_q[3:0]), .en(decoder_1_out1));
  _74HCT374 IRL (.D(ROM_data), .CP(decoder_3_out0), .nOE(not_4_out), .Q(PC0_io_2), .Zpeek(IRL_zpeek));
  _74HCT374 IRH (.D(ROM_data), .CP(decoder_3_out1), .nOE(1'b0), .Q(IRH_q));  // open: Zpeek
  _74HCT374 IN1 (.D(PC0_io_2), .CP(decoder_3_out6), .nOE(1'b0), .Q(IN1_q));  // open: Zpeek
  // Probe on IRL_zpeek
  // Probe on IRH_q
  _74HCT374 TMP (.D(PC0_io_2), .CP(decoder_3_out3), .nOE(not_7_out), .Q(PC0_io_2), .Zpeek(TMP_zpeek));
  _74HCT374 A (.D(PC0_io_2), .CP(decoder_3_out8), .nOE(not_12_out), .Q(PC0_io_2), .Zpeek(A_zpeek));
  _74HCT374 B (.D(PC0_io_2), .CP(decoder_3_out9), .nOE(not_13_out), .Q(PC0_io_2), .Zpeek(B_zpeek));
  // Probe on TMP_zpeek
  // Probe on A_zpeek
  // Probe on B_zpeek
  _74HCT374 C (.D(PC0_io_2), .CP(decoder_3_out10), .nOE(not_14_out), .Q(PC0_io_2), .Zpeek(C_zpeek));
  // Probe on C_zpeek
  // Probe on IN1_q
  _74HCT374 ADDR (.D(PC0_io_2), .CP(decoder_3_out7), .nOE(1'b0), .Q(ADDR_q));  // open: Zpeek
  // Probe on PC0_io_2
  // Probe on IRH_q[7:5]
  // Probe on {{11{1'b0}}, ADDR_q}
  AS6C4008 as6c4008_1 (
    .D(PC0_io_2), .A({{11{1'b0}}, ADDR_q}), .nCE(1'b0), .nOE(not_8_out), .nWE(not_20_out), .D_2(PC0_io_2));
  not not_20 (not_20_out, decoder_3_out4);
  ROM #(.addrWidth(19), .Select("high")) ALU_LUT (.addr({IRH_q[7:5], IN1_q, PC0_io_2}), .data(ALU_LUT_data));
  _74HCT374 ALU (.D(ALU_LUT_data), .CP(decoder_3_out2), .nOE(not_6_out), .Q(PC0_io_2));  // open: Zpeek
  TTY #(.trigger("falling")) tty_1 (.data(PC0_io_2[6:0]), .clk(decoder_3_out14));  // open: we, clr
  Pull_Resistor pull_resistor_1 (.node(controlled_buffer_1_out[7]));
  assign controlled_buffer_1_out = decoder_3_out13 ? PC0_io_2 : 8'bz;  // Controlled_Buffer controlled_buffer_1
  Keyboard keyboard_1 (
    .clk(key_ctrl_1_key_clk), .re(key_ctrl_1_key_read_en), .avail(keyboard_1_avail), .data(keyboard_1_data));  // open: clr
  key_ctrl key_ctrl_1 (
    .key_avail(keyboard_1_avail), .discard(controlled_buffer_1_out[7]), .key_clk(key_ctrl_1_key_clk),
    .key_read_en(key_ctrl_1_key_read_en), .rdy(key_ctrl_1_rdy[7]));
  assign PC0_io_2 = not_21_out ? {key_ctrl_1_rdy[7], keyboard_1_data} : 8'bz;  // Controlled_Buffer controlled_buffer_2
  not not_21 (not_21_out, not_11_out);

  // Notes on the sheet:
  //   contents of ROM (hex, n*v repeats v):
  //   0 2 48 0 0 5a 69 0 0 5a a 0 0 5a ff 3
  //   contents of uROM (hex, n*v repeats v):
  //   60 b 3c 61 86 2 28 33 3c 55*3f 60 b 3c 61 86 2 28 33 3c 55*3f 60 b 3c 61 86 2 28 33 3c 55*3f 60 b 3c
  //   61 86 2 28 33 3c 55*3f 60 b 3c 61 86 2 28 33 3c 55*3f 60 b 3c 61 86 2 28 33 3c 55*3f 60 b 3c 61 86 2
  //   28 33 3c 55*3f 60 b 3c 61 86 2 28 33 3c 55*3f 60 b 3c 61 86 2 28 33 3c 55*3f 60 b 3c 61 86 2 28 33
  //   3c 55*3f 60 b 3c 61 86 2 28 33 3c 55*3f 60 b 3c 61 86 2 28 33 3c 55*3f 60 b 3c 61 86 2 28 33 3c
  //   55*3f 60 b 3c 61 86 2 28 33 3c 55*3f 60 b 3c 61 86 2 28 33 3c 55*3f 60 b 3c 61 86 2 28 33 3c 55*3f
  //   60 b 3c 61 86 2 28 33 3c 55*3f 60 b 3c 61 86 2 28 33 3c 55*3f 60 b 3c 61 86 2 28 33 3c 55*3f 60 b 3c
  //   61 86 2 28 33 3c 55*3f 60 b 3c 61 86 2 28 33 3c 55*3f 60 b 3c 61 86 2 28 33 3c 55*3f 60 b 3c 61 86 2
  //   28 33 3c 55*3f 60 b 3c 61 86 2 28 33 3c 55*3f 60 b 3c 61 86 2 28 33 3c 55*3f 60 b 3c 61 86 2 28 33
  //   3c 55*3f 60 b 3c 61 86 2 28 33 3c 55*3f 60 b 3c 61 86 2 28 33 3c 55*3f 60 b 3c 61 86 2 28 33 3c
  //   55*3f 60 b 3c 61 86 2 28 33 3c 55*3f 60 b 3c 61 86 2 28 33 3c 55*3f 60 b 3c 61 86 2 28 33 3c 55*3f
  //   60 b 3c 61 86 2 28 33 3c 55*3f 60 b 3c 61 86 2 28 33 3c 55*3f 60 b 3c 61 86 2 28 33 3c 55*3f 60 b 3c
  //   61 86 2 28 33 3c 55*3f 60 b 3c 61 86 2 28 33 3c 55*3f 60 b 3c 61 86 2 28 33 3c 55*3f 60 b 3c 61 86 2
  //   28 33 3c 55*3f 60 b 3c 61 86 2 28 33 3c 55*3f 60 b 3c 61 86 2 28 33 3c 55*3f 60 b 3c 61 86 2 28 33
  //   3c 55*3f 60 b 3c 61 86 2 28 33 3c 55*3f 60 b 3c 61 86 2 28 33 3c 55*3f 60 b 3c 61 86 2 28 33 3c
  //   55*3f 60 b 3c 61 86 2 28 33 3c 55*3f 60 b 3c 61 86 2 28 33 3c 55*3f 60 b 3c 61 86 2 28 33 3c 55*3f
  //   60 b 3c 61 86 2 28 33 3c 55*3f 60 b 3c 61 86 2 28 33 3c 55*3f 60 b 3c 61 86 2 28 33 3c 55*3f 60 b 3c
  //   61 86 2 28 33 3c 55*3f 60 b 3c 61 86 2 28 33 3c 55*3f 60 b 3c 61 86 2 28 33 3c 55*3f 60 b 3c 61 86 2
  //   28 33 3c 55*3f 60 b 3c 61 86 2 28 33 3c 55*3f 60 b 3c 61 86 2 28 33 3c 55*3f 60 b 3c 61 86 2 28 33
  //   3c 55*3f 60 b 3c 61 86 2 28 33 3c 55*3f 60 b 3c 61 86 2 28 33 3c 55*3f 60 b 3c 61 86 2 28 33 3c
  //   55*3f 60 b 3c 61 86 2 28 33 3c 55*3f 60 b 3c 61 86 2 28 33 3c 55*3f 60 b 3c 61 86 2 28 33 3c 55*3f
  //   60 b 3c 61 86 2 28 33 3c 55*3f 60 b 3c 61 86 2 28 33 3c 55*3f 60 b 3c 61 86 2 28 33 3c 55*3f 60 b 3c
  //   61 86 2 28 33 3c 55*3f 60 b 3c 61 86 2 28 33 3c 55*3f 60 b 3c 61 86 2 28 33 3c 55*3f 60 b 3c 61 86 2
  //   28 33 3c 55*3f 60 b 3c 61 86 2 28 33 3c 55*3f 60 b 3c 61 86 2 28 33 3c 55*3f 60 b 3c 61 86 2 28 33
  //   3c 55*3f 60 b 3c 61 86 2 28 33 3c 55*3f 60 b 3c 61 86 2 28 33 3c 55*3f 60 b 3c 61 86 2 28 33 3c
  //   55*3f 60 b 3c 61 86 2 28 33 3c 55*3f 60 b 3c 61 86 2 28 33 3c 55*3f 60 b 3c 61 86 2 28 33 3c 55*3f
  //   60 b 3c 61 86 2 28 33 3c 55*3f 60 b 3c 61 86 2 28 33 3c 55*3f 60 b 3c 61 86 2 28 33 3c 55*3f 60 b 3c
  //   61 86 2 28 33 3c 55*3f 60 b 3c 61 86 2 28 33 3c 55*3f 60 b 3c 61 86 2 28 33 3c 55*3f 60 b 3c 61 86 2
  //   28 33 3c 55*3f 60 b 3c 61 86 2 28 33 3c 55*3f 60 b 3c 61 86 2 28 33 3c 55*3f 60 b 3c 61 86 2 28 33
  //   3c 55*3f 60 b 3c 61 86 2 28 33 3c 55*3f 60 b 3c 61 86 2 28 33 3c 55*3f 60 b 3c 61 86 2 28 33 3c
  //   55*3f 60 b 3c 61 86 2 28 33 3c 55*3f 60 b 3c 61 86 2 28 33 3c 55*3f 60 b 3c 61 86 2 28 33 3c 55*3f
  //   60 b 3c 61 86 2 28 33 3c 55*3f 60 b 3c 61 86 2 28 33 3c 55*3f 60 b 3c 61 86 2 28 33 3c 55*3f 60 b 3c
  //   61 86 2 28 33 3c 55*3f 60 b 3c 61 86 2 28 33 3c 55*3f 60 b 3c 61 86 2 28 33 3c 55*3f 60 b 3c 61 86 2
  //   28 33 3c 55*3f 60 b 3c 61 86 2 28 33 3c 55*3f 60 b 3c 61 86 2 28 33 3c 55*3f 60 b 3c 61 86 2 28 33
  //   3c 55*3f 60 b 3c 61 86 2 28 33 3c 55*3f 60 b 3c 61 86 2 28 33 3c 55*3f 60 b 3c 61 86 2 28 33 3c
  //   55*3f 60 b 3c 61 86 2 28 33 3c 55*3f 60 b 3c 61 86 2 28 33 3c 55*3f 60 b 3c 61 86 2 28 33 3c 55*3f
  //   60 b 3c 61 86 2 28 33 3c 55*3f 60 b 3c 61 86 2 28 33 3c 55*3f 60 b 3c 61 86 2 28 33 3c 55*3f 60 b 3c
  //   61 86 2 28 33 3c 55*3f 60 b 3c 61 86 2 28 33 3c 55*3f 60 b 3c 61 86 2 28 33 3c 55*3f 60 b 3c 61 86 2
  //   28 33 3c 55*3f 60 b 3c 61 86 2 28 33 3c 55*3f 60 b 3c 61 86 2 28 33 3c 55*3f 60 b 3c 61 86 2 28 33
  //   3c 55*3f 60 b 3c 61 86 2 28 33 3c 55*3f 60 b 3c 61 86 2 28 33 3c 55*3f 60 b 3c 61 86 2 28 33 3c
  //   55*3f 60 b 3c 61 86 2 28 33 3c 55*3f 60 b 3c 61 86 2 28 33 3c 55*3f 60 b 3c 61 86 2 28 33 3c 55*3f
  //   60 b 3c 61 86 2 28 33 3c 55*3f 6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
  //   contents of ALU_LUT (hex, n*v repeats v):
  //   0 1 2 3 4 5 6 7 8 9 a b c d e f 10 11 12 13 14 15 16 17 18 19 1a 1b 1c 1d 1e 1f 20 21 22 23 24 25 26
  //   27 28 29 2a 2b 2c 2d 2e 2f 30 31 32 33 34 35 36 37 38 39 3a 3b 3c 3d 3e 3f 40 41 42 43 44 45 46 47
  //   48 49 4a 4b 4c 4d 4e 4f 50 51 52 53 54 55 56 57 58 59 5a 5b 5c 5d 5e 5f 60 61 62 63 64 65 66 67 68
  //   69 6a 6b 6c 6d 6e 6f 70 71 72 73 74 75 76 77 78 79 7a 7b 7c 7d 7e 7f 80 81 82 83 84 85 86 87 88 89
  //   8a 8b 8c 8d 8e 8f 90 91 92 93 94 95 96 97 98 99 9a 9b 9c 9d 9e 9f a0 a1 a2 a3 a4 a5 a6 a7 a8 a9 aa
  //   ab ac ad ae af b0 b1 b2 b3 b4 b5 b6 b7 b8 b9 ba bb bc bd be bf c0 c1 c2 c3 c4 c5 c6 c7 c8 c9 ca cb
  //   cc cd ce cf d0 d1 d2 d3 d4 d5 d6 d7 d8 d9 da db dc dd de df e0 e1 e2 e3 e4 e5 e6 e7 e8 e9 ea eb ec
  //   ed ee ef f0 f1 f2 f3 f4 f5 f6 f7 f8 f9 fa fb fc fd fe ff 0 1 2 3 4 5 6 7 8 9 a b c d e f 10 11 12 13
  //   14 15 16 17 18 19 1a 1b 1c 1d 1e 1f 20 21 22 23 24 25 26 27 28 29 2a 2b 2c 2d 2e 2f 30 31 32 33 34
  //   35 36 37 38 39 3a 3b 3c 3d 3e 3f 40 41 42 43 44 45 46 47 48 49 4a 4b 4c 4d 4e 4f 50 51 52 53 54 55
  //   56 57 58 59 5a 5b 5c 5d 5e 5f 60 61 62 63 64 65 66 67 68 69 6a 6b 6c 6d 6e 6f 70 71 72 73 74 75 76
  //   77 78 79 7a 7b 7c 7d 7e 7f 80 81 82 83 84 85 86 87 88 89 8a 8b 8c 8d 8e 8f 90 91 92 93 94 95 96 97
  //   98 99 9a 9b 9c 9d 9e 9f a0 a1 a2 a3 a4 a5 a6 a7 a8 a9 aa ab ac ad ae af b0 b1 b2 b3 b4 b5 b6 b7 b8
  //   b9 ba bb bc bd be bf c0 c1 c2 c3 c4 c5 c6 c7 c8 c9 ca cb cc cd ce cf d0 d1 d2 d3 d4 d5 d6 d7 d8 d9
  //   da db dc dd de df e0 e1 e2 e3 e4 e5 e6 e7 e8 e9 ea eb ec ed ee ef f0 f1 f2 f3 f4 f5 f6 f7 f8 f9 fa
  //   fb fc fd fe ff 0 1 2 3 4 5 6 7 8 9 a b c d e f 10 11 12 13 14 15 16 17 18 19 1a 1b 1c 1d 1e 1f 20 21
  //   22 23 24 25 26 27 28 29 2a 2b 2c 2d 2e 2f 30 31 32 33 34 35 36 37 38 39 3a 3b 3c 3d 3e 3f 40 41 42
  //   43 44 45 46 47 48 49 4a 4b 4c 4d 4e 4f 50 51 52 53 54 55 56 57 58 59 5a 5b 5c 5d 5e 5f 60 61 62 63
  //   64 65 66 67 68 69 6a 6b 6c 6d 6e 6f 70 71 72 73 74 75 76 77 78 79 7a 7b 7c 7d 7e 7f 80 81 82 83 84
  //   85 86 87 88 89 8a 8b 8c 8d 8e 8f 90 91 92 93 94 95 96 97 98 99 9a 9b 9c 9d 9e 9f a0 a1 a2 a3 a4 a5
  //   a6 a7 a8 a9 aa ab ac ad ae af b0 b1 b2 b3 b4 b5 b6 b7 b8 b9 ba bb bc bd be bf c0 c1 c2 c3 c4 c5 c6
  //   c7 c8 c9 ca cb cc cd ce cf d0 d1 d2 d3 d4 d5 d6 d7 d8 d9 da db dc dd de df e0 e1 e2 e3 e4 e5 e6 e7
  //   e8 e9 ea eb ec ed ee ef f0 f1 f2 f3 f4 f5 f6 f7 f8 f9 fa fb fc fd fe ff 0 1 2 3 4 5 6 7 8 9 a b c d
  //   e f 10 11 12 13 14 15 16 17 18 19 1a 1b 1c 1d 1e 1f 20 21 22 23 24 25 26 27 28 29 2a 2b 2c 2d 2e 2f
  //   30 31 32 33 34 35 36 37 38 39 3a 3b 3c 3d 3e 3f 40 41 42 43 44 45 46 47 48 49 4a 4b 4c 4d 4e 4f 50
  //   51 52 53 54 55 56 57 58 59 5a 5b 5c 5d 5e 5f 60 61 62 63 64 65 66 67 68 69 6a 6b 6c 6d 6e 6f 70 71
  //   72 73 74 75 76 77 78 79 7a 7b 7c 7d 7e 7f 80 81 82 83 84 85 86 87 88 89 8a 8b 8c 8d 8e 8f 90 91 92
  //   93 94 95 96 97 98 99 9a 9b 9c 9d 9e 9f a0 a1 a2 a3 a4 a5 a6 a7 a8 a9 aa ab ac ad ae af b0 b1 b2 b3
  //   b4 b5 b6 b7 b8 b9 ba bb bc bd be bf c0 c1 c2 c3 c4 c5 c6 c7 c8 c9 ca cb cc cd ce cf d0 d1 d2 d3 d4
  //   d5 d6 d7 d8 d9 da db dc dd de df e0 e1 e2 e3 e4 e5 e6 e7 e8 e9 ea eb ec ed ee ef f0 f1 f2 f3 f4 f5
  //   f6 f7 f8 f9 fa fb fc fd fe ff 0 1 2 3 4 5 6 7 8 9 a b c d e f 10 11 12 13 14 15 16 17 18 19 1a 1b 1c
  //   1d 1e 1f 20 21 22 23 24 25 26 27 28 29 2a 2b 2c 2d 2e 2f 30 31 32 33 34 35 36 37 38 39 3a 3b 3c 3d
  //   3e 3f 40 41 42 43 44 45 46 47 48 49 4a 4b 4c 4d 4e 4f 50 51 52 53 54 55 56 57 58 59 5a 5b 5c 5d 5e
  //   5f 60 61 62 63 64 65 66 67 68 69 6a 6b 6c 6d 6e 6f 70 71 72 73 74 75 76 77 78 79 7a 7b 7c 7d 7e 7f
  //   80 81 82 83 84 85 86 87 88 89 8a 8b 8c 8d 8e 8f 90 91 92 93 94 95 96 97 98 99 9a 9b 9c 9d 9e 9f a0
  //   a1 a2 a3 a4 a5 a6 a7 a8 a9 aa ab ac ad ae af b0 b1 b2 b3 b4 b5 b6 b7 b8 b9 ba bb bc bd be bf c0 c1
  //   c2 c3 c4 c5 c6 c7 c8 c9 ca cb cc cd ce cf d0 d1 d2 d3 d4 d5 d6 d7 d8 d9 da db dc dd de df e0 e1 e2
  //   e3 e4 e5 e6 e7 e8 e9 ea eb ec ed ee ef f0 f1 f2 f3 f4 f5 f6 f7 f8 f9 fa fb fc fd fe ff 0 1 2 3 4 5 6
  //   7 8 9 a b c d e f 10 11 12 13 14 15 16 17 18 19 1a 1b 1c 1d 1e 1f 20 21 22 23 24 25 26 27 28 29 2a
  //   2b 2c 2d 2e 2f 30 31 32 33 34 35 36 37 38 39 3a 3b 3c 3d 3e 3f 40 41 42 43 44 45 46 47 48 49 4a 4b
  //   4c 4d 4e 4f 50 51 52 53 54 5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
endmodule

module mmu (
  input  [7:0] data_in,
  input  [6:0] key_char,
  input  key_rdy,
  input  [23:0] addr,
  input  store,
  input  clk,
  output key_discard,
  output [6:0] ttydata,
  output ttyclk,
  output [7:0] data_out
);

  wire and_1_out, and_2_out, and_3_out, comparator_1_eq, comparator_1_gt, comparator_1_lt, not_1_out;
  wire [7:0] controlled_buffer_4_out;

  assign data_out = store ? data_in : 8'bz;  // Controlled_Buffer controlled_buffer_1
  Comparator #(.width(24)) comparator_1 (
    .a(24'h1), .b(addr), .gt(comparator_1_gt), .eq(comparator_1_eq), .lt(comparator_1_lt));
  not not_1 (not_1_out, store);
  assign data_out = and_1_out ? {key_rdy, key_char} : 8'bz;  // Controlled_Buffer controlled_buffer_2
  and and_1 (and_1_out, comparator_1_gt, not_1_out);
  assign data_out = and_2_out ? 8'hcc : 8'bz;  // Controlled_Buffer controlled_buffer_3
  and and_2 (and_2_out, comparator_1_eq, not_1_out);
  assign controlled_buffer_4_out = store ? data_out : 8'bz;  // Controlled_Buffer controlled_buffer_4
  RAM #(.addrWidth(24), .Select("high")) ram_1 (
    .addr(addr), .data(controlled_buffer_4_out), .clk(clk), .ld(not_1_out));  // open: sel, clr
  assign data_out = and_3_out ? controlled_buffer_4_out : 8'bz;  // Controlled_Buffer controlled_buffer_5
  and and_3 (and_3_out, comparator_1_lt, not_1_out);
  and and_4 (key_discard, data_out[7], store, clk, comparator_1_gt);
  and and_5 (ttyclk, comparator_1_eq, store, clk);

  assign ttydata = data_out[6:0];

  // Notes on the sheet:
  //   addr == 1
  //   addr > 1
  //   addr == 0
endmodule

module key_ctrl (
  input  key_avail,
  input  discard,
  output key_clk,
  output key_read_en,
  output rdy
);

  wire and_1_out, and_3_out, and_4_out, clock_1_out, d_ff_1_q, d_ff_2_q, decoder_1_out0, decoder_1_out1,
       decoder_1_out2, decoder_1_out3, decoder_1_out4;
  wire [2:0] counter_1_q;

  Clock clock_1 (.out(clock_1_out));
  Decoder #(.select(3), .disabled(0), .enable("false")) decoder_1 (
    .out0(decoder_1_out0), .out1(decoder_1_out1), .out2(decoder_1_out2), .out3(decoder_1_out3),
    .out4(decoder_1_out4), .sel(counter_1_q));  // open: out5, out6, out7
  Counter #(.width(3), .max('h4), .trigger("falling"), .behavior("old")) counter_1 (
    .Q(counter_1_q), .clk(clock_1_out));  // open: load, D, count, carry, clr, preset
  or or_1 (key_clk, decoder_1_out0, and_1_out);
  and and_1 (and_1_out, decoder_1_out2, d_ff_2_q);
  or or_2 (key_read_en, decoder_1_out1, decoder_1_out2);
  D_Flip_Flop d_ff_1 (.clk(and_1_out), .D(1'b1), .Q(d_ff_1_q), .reset(and_4_out));  // open: Qn, preset
  D_Flip_Flop d_ff_2 (.clk(discard), .D(1'b1), .Q(d_ff_2_q), .reset(and_4_out));  // open: Qn, preset
  and and_2 (rdy, key_avail, ~and_3_out);  // AND_Gate
  and and_3 (and_3_out, d_ff_1_q, decoder_1_out3);
  and and_4 (and_4_out, d_ff_1_q, decoder_1_out4);
endmodule

module regs (
  input  [3:0] D,
  input  [3:0] index,
  input  W,
  input  R,
  input  ADDR_CLK,
  output [3:0] QLO,
  output [3:0] QHI,
  output [3:0] Q,
  output [23:0] extADDR,
  output [7:0] ADDR
);

  wire and_1_out, and_2_out, not_1_out, sn74ls156_1__1y0, sn74ls156_1__1y1, sn74ls156_1__1y2,
       sn74ls156_1__1y3, sn74ls156_1__2y0, sn74ls156_1__2y1, sn74ls156_1__2y2, sn74ls156_1__2y3;

  SN74LS156 sn74ls156_1 (
    .n1G(W), ._1C(1'b1), .SEL({index[3], index[0]}), .n2G(R), ._2C(1'b1), ._1Y0(sn74ls156_1__1y0),
    ._1Y1(sn74ls156_1__1y1), ._1Y2(sn74ls156_1__1y2), ._1Y3(sn74ls156_1__1y3), ._2Y0(sn74ls156_1__2y0),
    ._2Y1(sn74ls156_1__2y1), ._2Y2(sn74ls156_1__2y2), ._2Y3(sn74ls156_1__2y3));
  and and_1 (and_1_out, sn74ls156_1__2y0, sn74ls156_1__2y1);
  and and_2 (and_2_out, sn74ls156_1__2y2, sn74ls156_1__2y3);
  SN74LS670 LO1 (.W(index[2:1]), .nGW(sn74ls156_1__1y0), .R(index[2:1]), .nGR(and_1_out), .IO(D), .IO_2(QLO));
  SN74LS670 HI1 (.W(index[2:1]), .nGW(sn74ls156_1__1y1), .R(index[2:1]), .nGR(and_1_out), .IO(D), .IO_2(QHI));
  SN74LS670 LO2 (.W(index[2:1]), .nGW(sn74ls156_1__1y2), .R(index[2:1]), .nGR(and_2_out), .IO(D), .IO_2(QLO));
  SN74LS670 HI2 (.W(index[2:1]), .nGW(sn74ls156_1__1y3), .R(index[2:1]), .nGR(and_2_out), .IO(D), .IO_2(QHI));
  Multiplexer #(.width(4)) multiplexer_1 (.in0(QLO), .in1(QHI), .out(D), .sel(index[0]), .en(not_1_out));
  not not_1 (not_1_out, R);
  _74HCT377 u_74hct377_1 (.D({QHI, QLO}), .nEN(sn74ls156_1__2y0), .CLK(ADDR_CLK), .Q(extADDR[7:0]));
  _74HCT377 u_74hct377_2 (.D({QHI, QLO}), .nEN(sn74ls156_1__2y1), .CLK(ADDR_CLK), .Q(extADDR[15:8]));
  _74HCT377 u_74hct377_3 (.D({QHI, QLO}), .nEN(sn74ls156_1__2y2), .CLK(ADDR_CLK), .Q(extADDR[23:16]));
  _74HCT377 u_74hct377_4 (.D({QHI, QLO}), .nEN(sn74ls156_1__2y3), .CLK(ADDR_CLK), .Q(ADDR));

  assign Q = D;

  // Notes on the sheet:
  //   W: pull=up
  //   R: pull=up
endmodule

module SN74LS670 (
  input  [1:0] W,
  input  nGW,
  input  [1:0] R,
  input  nGR,
  input  [3:0] IO,
  output [3:0] IO_2
);

  wire decoder_1_out0, decoder_1_out1, decoder_1_out2, decoder_1_out3, decoder_2_out0, decoder_2_out1,
       decoder_2_out2, decoder_2_out3, not_1_out;
  wire [3:0] register_1_q, register_2_q, register_3_q, register_4_q;

  not not_1 (not_1_out, nGR);
  Decoder #(.select(2), .disabled(0), .enable("false")) decoder_1 (
    .out0(decoder_1_out0), .out1(decoder_1_out1), .out2(decoder_1_out2), .out3(decoder_1_out3), .sel(W));
  Decoder #(.select(2), .disabled(0)) decoder_2 (
    .out0(decoder_2_out0), .out1(decoder_2_out1), .out2(decoder_2_out2), .out3(decoder_2_out3), .sel(R),
    .en(not_1_out));
  Register #(.width(4), .Select("low")) register_1 (
    .D(IO), .en(decoder_1_out0), .Q(register_1_q), .clk(nGW));  // open: clr
  Register #(.width(4), .Select("low")) register_2 (
    .D(IO), .en(decoder_1_out1), .Q(register_2_q), .clk(nGW));  // open: clr
  Register #(.width(4), .Select("low")) register_3 (
    .D(IO), .en(decoder_1_out2), .Q(register_3_q), .clk(nGW));  // open: clr
  Register #(.width(4), .Select("low")) register_4 (
    .D(IO), .en(decoder_1_out3), .Q(register_4_q), .clk(nGW));  // open: clr
  assign IO = decoder_2_out0 ? register_1_q : 4'bz;  // Controlled_Buffer controlled_buffer_1
  assign IO = decoder_2_out1 ? register_2_q : 4'bz;  // Controlled_Buffer controlled_buffer_2
  assign IO = decoder_2_out2 ? register_3_q : 4'bz;  // Controlled_Buffer controlled_buffer_3
  assign IO = decoder_2_out3 ? register_4_q : 4'bz;  // Controlled_Buffer controlled_buffer_4

  assign IO_2 = IO;
endmodule

module SN74LS156 (
  input  n1G,
  input  _1C,
  input  [1:0] SEL,
  input  n2G,
  input  _2C,
  output _1Y0,
  output _1Y1,
  output _1Y2,
  output _1Y3,
  output _2Y0,
  output _2Y1,
  output _2Y2,
  output _2Y3
);

  wire and_1_out, and_2_out, decoder_1_out0, decoder_1_out1, decoder_1_out2, decoder_1_out3, decoder_2_out0,
       decoder_2_out1, decoder_2_out2, decoder_2_out3;

  and and_1 (and_1_out, ~n1G, _1C);  // AND_Gate
  and and_2 (and_2_out, ~n2G, _2C);  // AND_Gate
  Decoder #(.select(2), .disabled(0), .enable("false")) decoder_1 (
    .out0(decoder_1_out0), .out1(decoder_1_out1), .out2(decoder_1_out2), .out3(decoder_1_out3), .sel(SEL));
  Decoder #(.select(2), .disabled(0), .enable("false")) decoder_2 (
    .out0(decoder_2_out0), .out1(decoder_2_out1), .out2(decoder_2_out2), .out3(decoder_2_out3), .sel(SEL));
  Pull_Resistor #(.pull(1)) pull_resistor_1 (.node(_1Y2));
  Pull_Resistor #(.pull(1)) pull_resistor_2 (.node(_1Y0));
  Pull_Resistor #(.pull(1)) pull_resistor_3 (.node(_1Y1));
  assign _1Y0 = and_1_out ? ~decoder_1_out0 : 1'bz;  // Controlled_Inverter controlled_inverter_1
  assign _1Y1 = and_1_out ? ~decoder_1_out1 : 1'bz;  // Controlled_Inverter controlled_inverter_2
  assign _1Y2 = and_1_out ? ~decoder_1_out2 : 1'bz;  // Controlled_Inverter controlled_inverter_3
  Pull_Resistor #(.pull(1)) pull_resistor_4 (.node(_2Y2));
  Pull_Resistor #(.pull(1)) pull_resistor_5 (.node(_2Y0));
  Pull_Resistor #(.pull(1)) pull_resistor_6 (.node(_2Y1));
  assign _2Y0 = and_2_out ? ~decoder_2_out0 : 1'bz;  // Controlled_Inverter controlled_inverter_4
  assign _2Y1 = and_2_out ? ~decoder_2_out1 : 1'bz;  // Controlled_Inverter controlled_inverter_5
  assign _2Y2 = and_2_out ? ~decoder_2_out2 : 1'bz;  // Controlled_Inverter controlled_inverter_6
  Pull_Resistor #(.pull(1)) pull_resistor_7 (.node(_1Y3));
  assign _1Y3 = and_1_out ? ~decoder_1_out3 : 1'bz;  // Controlled_Inverter controlled_inverter_7
  Pull_Resistor #(.pull(1)) pull_resistor_8 (.node(_2Y3));
  assign _2Y3 = and_2_out ? ~decoder_2_out3 : 1'bz;  // Controlled_Inverter controlled_inverter_8
endmodule

module _74HCT377 (
  input  [7:0] D,
  input  nEN,
  input  CLK,
  output [7:0] Q
);

  wire not_1_out;

  not not_1 (not_1_out, nEN);
  Register #(.Select("low")) register_1 (.D(D), .en(not_1_out), .Q(Q), .clk(CLK));  // open: clr
endmodule

module _74HCT299 (
  input  [7:0] IO,
  input  S0,
  input  S1,
  input  CP,
  input  nMR,
  input  nOE1,
  input  nOE2,
  output [7:0] IO_2
);

  wire and_1_out, nor_1_out, not_1_out;
  wire [7:0] register_1_q;

  Pull_Resistor #(.pull(1)) pull_resistor_1 (.node(S0));
  Pull_Resistor #(.pull(1)) pull_resistor_2 (.node(S1));
  Pull_Resistor #(.pull(1)) pull_resistor_3 (.node(CP));
  Pull_Resistor #(.pull(1)) pull_resistor_4 (.node(nMR));
  Pull_Resistor #(.pull(1)) pull_resistor_5 (.node(nOE1));
  Pull_Resistor #(.pull(1)) pull_resistor_6 (.node(nOE2));
  and and_1 (and_1_out, S0, S1);
  not not_1 (not_1_out, nMR);
  nor nor_1 (nor_1_out, nOE1, and_1_out, nOE2);
  Register #(.Select("low")) register_1 (.D(IO), .en(and_1_out), .Q(register_1_q), .clk(CP), .clr(not_1_out));
  assign IO_2 = nor_1_out ? register_1_q : 8'bz;  // Controlled_Buffer controlled_buffer_1
endmodule

module _74LS593 (
  input  CCK,
  input  CCKEN,
  input  nCCKEN,
  input  nCCLR,
  input  nCLOAD,
  input  [7:0] IO,
  input  nRCKEN,
  input  RCK,
  input  G,
  input  nG,
  output [7:0] IO_2,
  output nRCO,
  output [7:0] peek
);

  wire and_1_out, and_2_out, and_3_out, and_4_out, and_5_out, and_6_out, and_7_out, and_8_out, and_9_out,
       and_10_out, and_11_out, and_12_out, and_13_out, and_14_out, and_15_out, and_16_out, comparator_1_eq,
       not_1_out, not_2_out, or_1_out, or_2_out, or_3_out, or_4_out, or_5_out, or_6_out, or_7_out, or_8_out,
       or_9_out, or_10_out;
  wire [7:0] adder_1_out, register_1_q;

  Pull_Resistor #(.pull(1)) pull_resistor_1 (.node(nCLOAD));
  Pull_Resistor #(.pull(1)) pull_resistor_2 (.node(nRCKEN));
  not not_1 (not_1_out, nRCKEN);
  Pull_Resistor #(.pull(1)) pull_resistor_3 (.node(RCK));
  Register #(.Select("low")) register_1 (.D(IO), .en(not_1_out), .Q(register_1_q), .clk(RCK));  // open: clr
  Pull_Resistor #(.pull(1)) pull_resistor_4 (.node(CCKEN));
  Pull_Resistor #(.pull(1)) pull_resistor_5 (.node(nCCKEN));
  Pull_Resistor #(.pull(1)) pull_resistor_6 (.node(nCCLR));
  and and_1 (and_1_out, register_1_q[0], ~nCLOAD);  // AND_Gate
  and and_2 (and_2_out, ~register_1_q[0], ~nCLOAD);  // AND_Gate
  and and_3 (and_3_out, register_1_q[1], ~nCLOAD);  // AND_Gate
  and and_4 (and_4_out, ~register_1_q[1], ~nCLOAD);  // AND_Gate
  and and_5 (and_5_out, register_1_q[2], ~nCLOAD);  // AND_Gate
  and and_6 (and_6_out, ~register_1_q[2], ~nCLOAD);  // AND_Gate
  and and_7 (and_7_out, register_1_q[3], ~nCLOAD);  // AND_Gate
  and and_8 (and_8_out, ~register_1_q[3], ~nCLOAD);  // AND_Gate
  and and_9 (and_9_out, register_1_q[4], ~nCLOAD);  // AND_Gate
  and and_10 (and_10_out, ~register_1_q[4], ~nCLOAD);  // AND_Gate
  and and_11 (and_11_out, register_1_q[5], ~nCLOAD);  // AND_Gate
  and and_12 (and_12_out, ~register_1_q[5], ~nCLOAD);  // AND_Gate
  and and_13 (and_13_out, register_1_q[6], ~nCLOAD);  // AND_Gate
  and and_14 (and_14_out, ~register_1_q[6], ~nCLOAD);  // AND_Gate
  and and_15 (and_15_out, register_1_q[7], ~nCLOAD);  // AND_Gate
  and and_16 (and_16_out, ~register_1_q[7], ~nCLOAD);  // AND_Gate
  Pull_Resistor #(.pull(1)) pull_resistor_7 (.node(CCK));
  or or_1 (or_1_out, CCKEN, ~nCCKEN);  // OR_Gate
  not not_2 (not_2_out, nCCLR);
  or or_2 (or_2_out, and_2_out, not_2_out);
  or or_3 (or_3_out, and_4_out, not_2_out);
  or or_4 (or_4_out, and_6_out, not_2_out);
  or or_5 (or_5_out, and_8_out, not_2_out);
  or or_6 (or_6_out, and_10_out, not_2_out);
  or or_7 (or_7_out, and_12_out, not_2_out);
  or or_8 (or_8_out, and_14_out, not_2_out);
  or or_9 (or_9_out, and_16_out, not_2_out);
  Register #(.width(1), .Select("low")) register_2 (
    .D(adder_1_out[0]), .en(or_1_out), .Q(peek[0]), .clk(CCK), .clr(or_2_out), .preset(and_1_out));  // open: cs
  Register #(.width(1), .Select("low")) register_3 (
    .D(adder_1_out[1]), .en(or_1_out), .Q(peek[1]), .clk(CCK), .clr(or_3_out), .preset(and_3_out));  // open: cs
  Register #(.width(1), .Select("low")) register_4 (
    .D(adder_1_out[2]), .en(or_1_out), .Q(peek[2]), .clk(CCK), .clr(or_4_out), .preset(and_5_out));  // open: cs
  Register #(.width(1), .Select("low")) register_5 (
    .D(adder_1_out[3]), .en(or_1_out), .Q(peek[3]), .clk(CCK), .clr(or_5_out), .preset(and_7_out));  // open: cs
  Register #(.width(1), .Select("low")) register_6 (
    .D(adder_1_out[4]), .en(or_1_out), .Q(peek[4]), .clk(CCK), .clr(or_6_out), .preset(and_9_out));  // open: cs
  Register #(.width(1), .Select("low")) register_7 (
    .D(adder_1_out[5]), .en(or_1_out), .Q(peek[5]), .clk(CCK), .clr(or_7_out), .preset(and_11_out));  // open: cs
  Register #(.width(1), .Select("low")) register_8 (
    .D(adder_1_out[6]), .en(or_1_out), .Q(peek[6]), .clk(CCK), .clr(or_8_out), .preset(and_13_out));  // open: cs
  Register #(.width(1), .Select("low")) register_9 (
    .D(adder_1_out[7]), .en(or_1_out), .Q(peek[7]), .clk(CCK), .clr(or_9_out), .preset(and_15_out));  // open: cs
  Adder adder_1 (.a(peek), .b(8'h1), .out(adder_1_out));  // open: cin, cout
  Pull_Resistor #(.pull(1)) pull_resistor_8 (.node(G));
  Pull_Resistor #(.pull(1)) pull_resistor_9 (.node(nG));
  assign IO_2 = or_10_out ? peek : 8'bz;  // Controlled_Buffer controlled_buffer_1
  or or_10 (or_10_out, G, ~nG);  // OR_Gate
  Comparator comparator_1 (.a(peek), .b({8{1'b1}}), .eq(comparator_1_eq));  // open: gt, lt
  not not_3 (nRCO, comparator_1_eq);

  // Notes on the sheet:
  //   nCCKEN: pull=up
  //   CCKEN: pull=up
  //   CCK: pull=up
  //   nCCLR: pull=up
  //   peek: pull=up
  //   nCLOAD: pull=up
  //   RCK: pull=up
  //   nRCKEN: pull=up
  //   nG: pull=up
  //   IO_2: pull=up
  //   G: pull=up
endmodule

module _74HCT374 (
  input  [7:0] D,
  input  CP,
  input  nOE,
  output [7:0] Q,
  output [7:0] Zpeek
);

  wire not_1_out;

  not not_1 (not_1_out, nOE);
  Register #(.Select("low")) register_1 (.D(D), .Q(Zpeek), .clk(CP));  // open: en, clr
  assign Q = not_1_out ? Zpeek : 8'bz;  // Controlled_Buffer controlled_buffer_1
endmodule

// RAM
module AS6C4008 (
  input  [7:0] D,
  input  [18:0] A,
  input  nCE,
  input  nOE,
  input  nWE,
  output [7:0] D_2
);

  wire nor_1_out, nor_2_out, not_1_out;

  RAM #(.addrWidth(19), .bus("asynch"), .Select("high")) RAM (.addr(A), .data(D), .ld(nor_2_out));  // open: sel, clr
  nor nor_1 (nor_1_out, nCE, nOE, nor_2_out);
  nor nor_2 (nor_2_out, nCE, nWE);
  assign D = not_1_out ? D_2 : 8'bz;  // Controlled_Buffer controlled_buffer_1
  assign D_2 = nor_1_out ? D : 8'bz;  // Controlled_Buffer controlled_buffer_2
  not not_1 (not_1_out, nor_1_out);
endmodule
