// Digital circuit SST39SF040.dig as structural Verilog
module SST39SF040 (
  input  CE,
  input  OE,
  input  WE,
  input  [18:0] A,
  output [7:0] DQ
);

  wire comparator_1_eq, comparator_2_eq, comparator_3_eq, comparator_4_eq, comparator_5_eq, comparator_6_eq,
       not_1_out, or_1_out, ramdualport_1_d;
  wire [7:0] multiplexer_1_out, ROM_d;

  Comparator #(.Bits(19)) comparator_1 (.a(A), .b(19'h5555), .eq(comparator_1_eq));  // open: gt, lt
  Comparator #(.Bits(8)) comparator_2 (.a(DQ), .b(8'haa), .eq(comparator_2_eq));  // open: gt, lt
  Comparator #(.Bits(19)) comparator_3 (.a(A), .b(19'h2aaa), .eq(comparator_3_eq));  // open: gt, lt
  Comparator #(.Bits(8)) comparator_4 (.a(DQ), .b(8'h55), .eq(comparator_4_eq));  // open: gt, lt
  Comparator #(.Bits(19)) comparator_5 (.a(A), .b(19'h5555), .eq(comparator_5_eq));  // open: gt, lt
  Comparator #(.Bits(8)) comparator_6 (.a(DQ), .b(8'ha0), .eq(comparator_6_eq));  // open: gt, lt
  // And and_1 has open pins: In_1=comparator_1_eq, In_2=comparator_2_eq, out=open
  // And and_2 has open pins: In_1=comparator_3_eq, In_2=comparator_4_eq, out=open
  // And and_3 has open pins: In_1=comparator_5_eq, In_2=comparator_6_eq, out=open
  not not_1 (not_1_out, CE);
  or or_1 (or_1_out, OE, CE);
  ROM #(.AddrBits(19), .isProgramMemory("true"), .Bits(8)) ROM (.A(A), .sel(not_1_out), .D(ROM_d));
  RAMSinglePortSel #(.AddrBits(19), .Bits(8)) ramsingleportsel_1 (.A(A), .CS(1'b0), .WE(1'b0), .OE(1'b0), .D(DQ));
  RAMDualPort #(.AddrBits(19)) ramdualport_1 (.A(A), .Din(1'b1), .str(1'b1), .C(1'b0), .ld(1'b1), .D(ramdualport_1_d));
  Multiplexer #(.Bits(8)) multiplexer_1 (.sel(ramdualport_1_d), .in_0(ROM_d), .in_1(DQ), .out(multiplexer_1_out));
  assign DQ = ~or_1_out ? multiplexer_1_out : 8'bz;  // DriverInvSel driverinvsel_1

  // Notes on the sheet:
  //   ROM loads rom.hex
endmodule

/* Test case:
CE_ OE_ DQ
1   X   Z
X   1   Z
*/
