// Digital circuit lcd.dig as structural Verilog
module lcd (
  input  clk,
  input  RW,
  input  [7:0] DB,
  input  E,
  input  RS
);

  wire and_1_out, and_2_out, and_3_out, comparator_1_lt, decoder_1_out_7, decoder_1_out_9, not_1_out,
       not_2_out, priorityencoder_1_any;
  wire [2:0] sub_1_s;
  wire [3:0] priorityencoder_1_num;
  wire [4:0] barrelshifter_1_out, CGROM_d;
  wire [7:0] AC_q, div_3_q;
  wire [10:0] DDRAM_d2;
  wire [12:0] counter_1_out, div_1_q, div_1_r, div_3_r;
  wire [12:2] div_2_q;
  wire [12:3] div_2_r;
  wire [12:6] div_3_q_2;

  PriorityEncoder #(.Selector_Bits(4)) priorityencoder_1 (
    .in0(DB[0]), .in1(DB[1]), .in2(DB[2]), .in3(DB[3]), .in4(DB[4]), .in5(DB[5]), .in6(DB[6]), .in7(DB[7]),
    .in8(RW), .in9(RS), .in10(1'b0), .in11(1'b0), .in12(1'b0), .in13(1'b0), .in14(1'b0), .in15(1'b0),
    .num(priorityencoder_1_num), .any(priorityencoder_1_any));
  Decoder #(.Selector_Bits(4)) decoder_1 (
    .sel(priorityencoder_1_num), .out_7(decoder_1_out_7), .out_9(decoder_1_out_9));  // open: out_0, out_1, out_2, out_3, out_4, out_5, out_6, out_8, out_10, out_11, out_12, out_13, out_14, out_15
  and and_1 (and_1_out, decoder_1_out_7, priorityencoder_1_any, E);
  and and_2 (and_2_out, decoder_1_out_9, priorityencoder_1_any, E);
  Register #(.Bits(8)) AC (.D({1'b0, DB[6:0]}), .C(and_1_out), .en(1'b1), .Q(AC_q));
  Counter #(.Bits(13)) counter_1 (.en(1'b1), .C(clk), .clr(1'b0), .out(counter_1_out));  // open: ovf
  RAMDualAccess #(.AddrBits(8), .Bits(8)) DDRAM (
    .str(not_1_out), .C(and_2_out), .ld(RW), .A1(AC_q), .Din1({1'b0, DB[6:0]}), .A2(div_3_q), .D1(DB),
    .D2(DDRAM_d2[10:3]));
  not not_1 (not_1_out, RW);
  Comparator #(.Bits(13)) comparator_1 (.a(counter_1_out), .b(13'hc80), .lt(comparator_1_lt));  // open: gt, eq
  // Probe P_i on counter_1_out
  Div #(.Bits(13)) div_1 (.a(counter_1_out), .b(13'h64), .q(div_1_q), .r(div_1_r));
  and and_3 (and_3_out, comparator_1_lt, clk);
  // Probe on DDRAM_d2
  ROM #(.AddrBits(11), .Bits(5)) CGROM (.A(DDRAM_d2), .sel(1'b1), .D(CGROM_d));
  // Probe P_R on div_1_q
  // Probe P_C on div_1_r
  Div #(.Bits(13)) div_2 (.a(div_1_q), .b(13'h8), .q({div_2_q, div_3_q[7:6]}), .r({div_2_r, DDRAM_d2[2:0]}));
  Div #(.Bits(13)) div_3 (.a(div_1_r), .b(13'h5), .q({div_3_q_2, div_3_q[5:0]}), .r(div_3_r));
  Sub #(.Bits(3)) sub_1 (.a(3'b100), .b(div_3_r[2:0]), .c_i(1'b0), .s(sub_1_s));  // open: c_o
  BarrelShifter #(.Bits(5), .barrelShifterMode("rotate"), .direction("right")) barrelshifter_1 (
    .in(CGROM_d), .shift(sub_1_s), .out(barrelshifter_1_out));
  // Probe C_R on {div_2_q, div_3_q[7:6]}
  // Probe C_C on {div_3_q_2, div_3_q[5:0]}
  // Probe D_R on DDRAM_d2[2:0]
  // Probe D_C on div_3_r[2:0]
  not not_2 (not_2_out, and_3_out);
  GraphicCard #(.graphicHeight(32), .graphicWidth(100)) graphiccard_1 (
    .A(counter_1_out), .str(1'b1), .C(not_2_out), .ld(1'b0), .B(1'b0), .D(barrelshifter_1_out[0]));

  // Notes on the sheet:
  //   clk: Hz: 276447232
  //   HD44780U
  //   AMC2004A
  //   contents of CGROM (hex, n*v repeats v):
  //   330*0,4*4,0,0,4,0,0,0,a,a,a,7*0,a,a,1f,a,1f,a,a,0,0,0,4,f,14,e
  //   ,5,1e,4,0,0,0,18,19,2,4,8,13,3,0,0,0,c,12,14,8,15,12,d,0,0,0,c
  //   ,4,8,7*0,2,4,8,8,8,4,2,0,0,0,8,4,2,2,2,4,8,4*0,4,15,e,15,4,5*0
  //   ,4,4,1f,4,4,8*0,c,4,8,6*0,1f,11*0,c,c,4*0,1,2,4,8,10,4*0,e,11
  //   ,13,15,19,11,e,0,0,0,4,c,4*4,e,0,0,0,e,11,1,2,4,8,1f,0,0,0,1f
  //   ,2,4,2,1,11,e,0,0,0,2,6,a,12,1f,2,2,0,0,0,1f,10,1e,1,1,11,e,0,0,0
  //   ,6,8,10,1e,11,11,e,0,0,0,1f,11,1,2,4,4,4,0,0,0,e,11,11,e,11,11
  //   ,e,0,0,0,e,11,11,f,1,2,c,4*0,c,c,0,c,c,5*0,c,c,0,c,4,8,0,0,0,2
  //   ,4,8,10,8,4,2,5*0,1f,0,1f,5*0,8,4,2,1,2,4,8,0,0,0,e,11,1,2,4,0
  //   ,4,0,0,0,e,11,1,d,15,15,e,0,0,0,e,11,11,11,1f,11,11,0,0,0,1e,11,11
  //   ,1e,11,11,1e,0,0,0,e,11,10,10,10,11,e,0,0,0,1c,12,11,11,11,12
  //   ,1c,0,0,0,1f,10,10,1e,10,10,1f,0,0,0,1f,10,10,1e,10,10,10,0,0,0
  //   ,e,11,10,17,11,11,f,0,0,0,11,11,11,1f,11,11,11,0,0,0,e,5*4,e,0,0,0
  //   ,7,4*2,12,c,0,0,0,11,12,14,18,14,12,11,0,0,0,6*10,1f,0,0,0,11
  //   ,1b,15,15,11,11,11,0,0,0,11,11,19,15,13,11,11,0,0,0,e,5*11,e,0,0,0
  //   ,1e,11,11,1e,10,10,10,0,0,0,e,11,11,11,15,12,d,0,0,0,1e,11,11
  //   ,1e,14,12,11,0,0,0,f,10,10,e,1,1,1e,0,0,0,1f,6*4,0,0,0,6*11,e
  //   ,0,0,0,5*11,a,4,0,0,0,11,11,11,15,15,15,a,0,0,0,11,11,a,4,a,11,11
  //   ,0,0,0,11,11,11,a,4,4,4,0,0,0,1f,1,2,4,8,10,1f,0,0,0,1c,5*10,1c
  //   ,0,0,0,11,a,1f,4,1f,4,4,0,0,0,e,5*2,e,0,0,0,4,a,11,13*0,1f,0,0,0
  //   ,8,4,2,9*0,e,1,f,11,f,0,0,0,10,10,16,19,11,11,1e,5*0,e,10,10,11
  //   ,e,0,0,0,1,1,d,13,11,11,f,5*0,e,11,1f,10,e,0,0,0,6,9,8,1c,8,8,8
  //   ,4*0,f,11,11,f,1,e,0,0,0,10,10,16,19,11,11,11,0,0,0,4,0,c,4,4,4
  //   ,e,0,0,0,2,0,6,2,2,12,c,0,0,0,10,10,12,14,18,14,12,0,0,0,c,5*4
  //   ,e,5*0,1a,15,15,11,11,5*0,16,19,11,11,11,5*0,e,11,11,11,e,5*0
  //   ,1e,11,1e,10,10,5*0,d,13,f,1,1,5*0,16,19,10,10,10,5*0,e,10,e,1
  //   ,1e,0,0,0,8,8,1c,8,8,9,6,5*0,11,11,11,13,d,5*0,11,11,11,a,4,5*0
  //   ,11,15,15,15,a,5*0,11,a,4,a,11,5*0,11,11,f,1,e,5*0,1f,2,4,8,1f
  //   ,0,0,0,2,4,4,8,4,4,2,0,0,0,7*4,0,0,0,8,4,4,2,4,4,8,4*0,4,2,1f
  //   ,2,4,5*0,4,8,1f,8,4,338*0,1c,14,1c,0,0,0,7,4,4,4,9*0,4,4,4,1c
  //   ,7*0,10,8,4,6*0,c,c,6*0,1f,1,1f,1,2,4,5*0,1f,1,6,4,8,5*0,2,4,c
  //   ,14,4,5*0,4,1f,11,1,6,5*0,1f,4,4,4,1f,5*0,2,1f,6,a,12,5*0,8,1f
  //   ,9,a,8,6*0,e,2,2,1f,5*0,1e,2,1e,2,1e,6*0,15,15,1,6,6*0,1f,6*0
  //   ,1f,1,5,6,4,4,8,0,0,0,1,2,4,c,14,4,4,0,0,0,4,1f,11,11,1,2,4,4*0
  //   ,1f,4*4,1f,0,0,0,2,1f,2,6,a,12,2,0,0,0,8,1f,4*9,12,0,0,0,4,1f
  //   ,4,1f,4,4,4,4*0,f,9,11,1,2,c,0,0,0,8,f,12,2,2,2,4,4*0,1f,4*1,1f
  //   ,0,0,0,a,1f,a,a,2,4,8,4*0,18,1,19,1,2,1c,4*0,1f,1,2,4,a,11,0,0,0
  //   ,8,1f,9,a,8,8,7,4*0,11,11,9,1,2,c,4*0,f,9,15,3,2,c,0,0,0,2,1c
  //   ,4,1f,4,4,8,4*0,15,15,15,1,2,4,0,0,0,e,0,1f,4,4,4,8,0,0,0,8,8,8
  //   ,c,a,8,8,0,0,0,4,4,1f,4,4,8,10,4*0,e,4*0,1f,4*0,1f,1,a,4,a,10
  //   ,0,0,0,4,1f,2,4,e,15,4,0,0,0,5*2,4,8,4*0,4,2,4*11,0,0,0,10,10
  //   ,1f,10,10,10,f,4*0,1f,1,1,1,2,c
endmodule

/* Test case:
RW DB_out
0  Z
*/
