// Digital circuit lutcomp.dig as structural Verilog
module lutcomp (
  input  RESET,
  input  clk,
  output HALT
);

  wire and_1_out, and_3_out, CLK_t, CLK_t_t, counter_1_ovf, decoder_1_out_0, decoder_1_out_1,
       decoder_1_out_2, decoder_1_out_3, decoder_1_out_4, decoder_1_out_5, decoder_1_out_6, decoder_1_out_7,
       io_1_io0_cp, io_1_io0_oe, io_1_io2_cp, io_1_io2_oe, io_1_io_avail, not_1_out, not_3_out, not_4_out,
       not_5_out, ps2_decoder_1_ps2_ready, ps2_encoder_1_ack, PS2_Keyboard_av, switch_1_b, TTYIN_av,
       ttymux_1_available, ttymux_1_key_clk, ttymux_1_term_clk, uc_1_a0_cp, uc_1_a0_oe, uc_1_a1_cp,
       uc_1_a1_oe, uc_1_a2_cp, uc_1_a2_oe, uc_1_addr_oe, uc_1_alu_cp, uc_1_alu_oe, uc_1_in1_cp,
       uc_1_io_rtw_oe, uc_1_iox_cp, uc_1_iox_data_oe, uc_1_iox_rtr_oe, uc_1_mem_cp, uc_1_mem_oe, uc_1_pc_inc,
       uc_1_pc_spe, uc_1_w_cp, uc_1_w_oe, uc_1_x_cp, uc_1_x_oe, uc_1_y_cp, uc_1_y_oe, uc_1_z_cp, uc_1_z_oe,
       undriven_2, undriven_3;
  wire [1:0] ttymux_1_in_source, uc_1_stage;
  wire [2:0] uc_1_alu_op, uc_1_io_sel;
  wire [3:0] uc_1_uaddr_3;
  wire [6:0] uc_1_uaddr;
  wire [7:0] counter_4_out, rom_1_d, ttymux_1_in_value, uc_1_data, uc_1_ir0, uc_1_uaddr_2, uc_1_udata,
       uc_1_uir0, uc_1_uir1, uc_1_upc;
  wire [9:0] counter_1_out;
  wire [15:0] counter_3_out, TTYIN_d;
  wire [15:7] PS2_Keyboard_d;
  wire [23:0] pc_1_pc, undriven;
  wire [63:0] counter_2_out;

  Keyboard PS2_Keyboard (.C(counter_1_ovf), .en(1'b1), .D({PS2_Keyboard_d, counter_1_out[9:3]}), .av(PS2_Keyboard_av));
  Counter #(.Bits(3)) counter_1 (
    .en(PS2_Keyboard_av), .C(ps2_encoder_1_ack), .clr(1'b0), .out(counter_1_out[2:0]), .ovf(counter_1_ovf));
  ROM #(.AddrBits(10), .Bits(8)) rom_1 (.A(counter_1_out), .sel(1'b1), .D(rom_1_d));
  and and_1 (and_1_out, CLK_t, PS2_Keyboard_av);
  and and_2 (CLK_t, clk, HALT);
  Stop stop_1 (.stop(~HALT));
  not not_1 (not_1_out, HALT);
  ps2_encoder ps2_encoder_1 (
    .CLK(and_1_out), .DATA(rom_1_d), .PS2_CLK(undriven_3), .PS2_DATA(undriven_2), .ACK(ps2_encoder_1_ack));
  Break #(.Cycles(1000000000)) break_1 (.brk(not_1_out));
  not not_2 (CLK_t_t, CLK_t);
  // Probe TickCount on counter_2_out
  Counter #(.Bits(64)) counter_2 (.en(1'b1), .C(CLK_t), .clr(1'b0), .out(counter_2_out));  // open: ovf
  ps2_decoder ps2_decoder_1 (
    .PS2_CP(io_1_io2_cp), .DATA(uc_1_data), .PS2_OE(io_1_io2_oe), .PS2_CLK(undriven_3),
    .PS2_DATA(undriven_2), .PS2_READY(ps2_decoder_1_ps2_ready));
  uc uc_1 (
    .CLK(CLK_t_t), .RESET(RESET), .INT_PENDING(io_1_io_avail), .DATA(uc_1_data), .ADDR_OE(uc_1_addr_oe),
    .ALU_OP(uc_1_alu_op), .PC_INC(uc_1_pc_inc), .IN1_CP(uc_1_in1_cp), .ALU_CP(uc_1_alu_cp),
    .MEM_CP(uc_1_mem_cp), .W_CP(uc_1_w_cp), .X_CP(uc_1_x_cp), .Y_CP(uc_1_y_cp), .Z_CP(uc_1_z_cp),
    .A0_CP(uc_1_a0_cp), .A1_CP(uc_1_a1_cp), .A2_CP(uc_1_a2_cp), .HALT(HALT), .ALU_OE(uc_1_alu_oe),
    .MEM_OE(uc_1_mem_oe), .IO_RTW_OE(uc_1_io_rtw_oe), .PC_SPE(uc_1_pc_spe), .W_OE(uc_1_w_oe),
    .X_OE(uc_1_x_oe), .Y_OE(uc_1_y_oe), .Z_OE(uc_1_z_oe), .uIR0(uc_1_uir0), .uIR1(uc_1_uir1),
    .uAddr({uc_1_uaddr_3, uc_1_uaddr_2, uc_1_uaddr}), .uPC(uc_1_upc), .stage(uc_1_stage), .uData(uc_1_udata),
    .IOX_CP(uc_1_iox_cp), .IOX_RTR_OE(uc_1_iox_rtr_oe), .A0_OE(uc_1_a0_oe), .A1_OE(uc_1_a1_oe),
    .A2_OE(uc_1_a2_oe), .IO_SEL(uc_1_io_sel), .IOX_DATA_OE(uc_1_iox_data_oe), .IR0(uc_1_ir0));  // open: UNUSED_5, UNUSED_F
  // Probe on ps2_decoder_1_ps2_ready
  not not_3 (not_3_out, uc_1_addr_oe);
  // Probe on uc_1_uir0
  // Probe on uc_1_uir1
  // Probe on uc_1_upc
  // Probe on uc_1_stage
  // Probe on uc_1_udata
  // Probe on uc_1_ir0
  and and_3 (and_3_out, uc_1_pc_inc, ~uc_1_pc_spe);  // And
  Switch switch_1 (.A(uc_1_pc_inc), .B(switch_1_b));
  pc pc_1 (.PC_INC(uc_1_pc_inc), .RESET(RESET), .PC_SPE(uc_1_pc_spe), .OE(not_3_out), .ADDR(undriven), .PC(pc_1_pc));
  not not_4 (not_4_out, uc_1_io_rtw_oe);
  Break #(.Cycles(1000000000)) break_2 (.brk(uc_1_iox_cp));
  not not_5 (not_5_out, uc_1_iox_rtr_oe);
  Counter #(.Bits(16)) counter_3 (.en(1'b1), .C(uc_1_pc_inc), .clr(1'b0), .out(counter_3_out));  // open: ovf
  Break #(.Cycles(10000000)) break_3 (.brk(switch_1_b));
  PullDown pulldown_1 (.out(switch_1_b));
  Break #(.Cycles(1000000000)) break_4 (.brk(not_4_out));
  // Probe $uPC on {uc_1_uaddr_3, uc_1_uaddr_2, uc_1_uaddr}
  // Probe on uc_1_uaddr
  // Probe $IR0 on uc_1_uaddr_2
  // Probe $FLAGS on uc_1_uaddr_3
  Break #(.Cycles(1000000000)) break_5 (.brk(not_5_out));
  io io_1 (
    .DATA(uc_1_data), .IO_SEL(uc_1_io_sel), .IO_OE(uc_1_iox_data_oe), .IO_CP(uc_1_iox_cp),
    .IO_AVAIL_OE(uc_1_iox_rtr_oe), .IO0_AVAIL(ttymux_1_available), .IO1_AVAIL(1'b0),
    .IO2_AVAIL(ps2_decoder_1_ps2_ready), .IO_AVAIL(io_1_io_avail), .IO0_CP(io_1_io0_cp),
    .IO0_OE(io_1_io0_oe), .IO2_CP(io_1_io2_cp), .IO2_OE(io_1_io2_oe));  // open: IO1_CP, IO1_OE
  Counter #(.Bits(8)) counter_4 (.en(1'b1), .C(and_3_out), .clr(1'b0), .out(counter_4_out));  // open: ovf
  // Probe PC on pc_1_pc
  RAMDualPort #(.AddrBits(16), .Bits(24)) PC_LOG (
    .A(counter_3_out), .Din(pc_1_pc), .str(1'b1), .C(uc_1_pc_inc), .ld(1'b0));  // open: D
  RAMDualPort #(.AddrBits(8), .Bits(24)) JMP_LOG (
    .A(counter_4_out), .Din(pc_1_pc), .str(1'b1), .C(and_3_out), .ld(1'b0));  // open: D
  memory memory_1 (
    .MEM_WE(uc_1_mem_cp), .ADDR_OE(uc_1_addr_oe), .A0_CP(uc_1_a0_cp), .A1_CP(uc_1_a1_cp), .A2_CP(uc_1_a2_cp),
    .MEM_OE(uc_1_mem_oe), .DATA(uc_1_data), .ADDR(undriven), .A0_OE(uc_1_a0_oe), .A1_OE(uc_1_a1_oe),
    .A2_OE(uc_1_a2_oe));
  // Probe ADDR on undriven
  // Probe DATA on uc_1_data
  ttymux ttymux_1 (
    .DATA(uc_1_data), .TTYIN_CP(io_1_io0_oe), .TTYIN_OE(io_1_io0_oe), .TTYOUT_CP(io_1_io0_cp),
    .KEY_D(TTYIN_d), .KEY_AV(TTYIN_av), .TERM_CLK(ttymux_1_term_clk), .KEY_CLK(ttymux_1_key_clk),
    .IN_SOURCE(ttymux_1_in_source), .IN_VALUE(ttymux_1_in_value), .AVAILABLE(ttymux_1_available));
  Keyboard TTYIN (.C(ttymux_1_key_clk), .en(1'b1), .D(TTYIN_d), .av(TTYIN_av));
  Terminal TTYOUT (.D(uc_1_data), .C(ttymux_1_term_clk), .en(1'b1));
  Decoder #(.Selector_Bits(3)) decoder_1 (
    .sel(uc_1_alu_op), .out_0(decoder_1_out_0), .out_1(decoder_1_out_1), .out_2(decoder_1_out_2),
    .out_3(decoder_1_out_3), .out_4(decoder_1_out_4), .out_5(decoder_1_out_5), .out_6(decoder_1_out_6),
    .out_7(decoder_1_out_7));
  alu alu_1 (
    .ALU_OP(uc_1_alu_op), .ALU_OE(uc_1_alu_oe), .ALU_CP(uc_1_alu_cp), .IN1_CP(uc_1_in1_cp), .DATA(uc_1_data));  // open: IN1, ALU_REG, ALU_RESULT
  \reg  W (.OE(uc_1_w_oe), .CP(uc_1_w_cp), .IO(uc_1_data));
  \reg  X (.OE(uc_1_x_oe), .CP(uc_1_x_cp), .IO(uc_1_data));
  \reg  Y (.OE(uc_1_y_oe), .CP(uc_1_y_cp), .IO(uc_1_data));
  \reg  Z (.OE(uc_1_z_oe), .CP(uc_1_z_cp), .IO(uc_1_data));
  // Probe AddLo on decoder_1_out_0
  // Probe AddHiNC on decoder_1_out_2
  // Probe Or on decoder_1_out_4
  // Probe And on decoder_1_out_6
  // Probe on ttymux_1_in_source
  // Probe on ttymux_1_in_value
  // Probe MulHi on decoder_1_out_1
  // Probe AddHiC on decoder_1_out_3
  // Probe Div on decoder_1_out_5
  // Probe Special on decoder_1_out_7

  // Notes on the sheet:
  //   RESET: default 1
  //   clk: Hz: 100000
  //   PS2 Keyboard
  //   rom_1 loads ascii_to_ps2.hex
  //   4A
  //   4B
  //   4Y
  //   6A
  //   6Y
  //   3A
  //   3Y
  //   TTY
endmodule

/* Test case:
RESET_ HALT_
0      1
*/
