// Digital circuit serial_rom.dig as structural Verilog
module serial_rom (
  input  SCLK,
  input  SI,
  input  CE,
  input  HOLD,
  output SO,
  output [2:0] \bit ,
  output [2:0] \byte 
);

  wire and_1_out, and_2_out, bitselector_1_out, comparator_1_eq, comparator_2_lt, d_ff_as_1_q,
       decoder_1_out_0, decoder_1_out_1, decoder_1_out_2, decoder_1_out_3, decoder_1_out_4, nor_1_out,
       not_1_out, not_2_out;
  wire [2:0] sub_1_s;
  wire [7:0] rom_1_d, shift_reg_1_q, shift_reg_2_q, shift_reg_3_q, shift_reg_4_q;
  wire [7:6] clks_out;
  wire [19:0] add_1_s, register_1_q;
  wire [22:0] counter_1_out;

  nor nor_1 (nor_1_out, not_1_out, CE);
  not not_1 (not_1_out, HOLD);
  and and_1 (and_1_out, nor_1_out, SCLK);
  Counter #(.Bits(8)) clks (.en(1'b1), .C(and_1_out), .clr(CE), .out({clks_out, \byte , \bit }));  // open: ovf
  Decoder #(.Selector_Bits(3)) decoder_1 (
    .sel(\byte ), .out_0(decoder_1_out_0), .out_1(decoder_1_out_1), .out_2(decoder_1_out_2),
    .out_3(decoder_1_out_3), .out_4(decoder_1_out_4));  // open: out_5, out_6, out_7
  Counter #(.Bits(23)) counter_1 (.en(d_ff_as_1_q), .C(not_2_out), .clr(CE), .out(counter_1_out));  // open: ovf
  // Probe on counter_1_out[22:3]
  shift_reg shift_reg_1 (.SCLK(and_1_out), .SIN(SI), .EN(decoder_1_out_0), .Q(shift_reg_1_q));  // open: OF
  shift_reg shift_reg_2 (.SCLK(and_1_out), .SIN(SI), .EN(decoder_1_out_1), .Q(shift_reg_2_q));  // open: OF
  shift_reg shift_reg_3 (.SCLK(and_1_out), .SIN(SI), .EN(decoder_1_out_2), .Q(shift_reg_3_q));  // open: OF
  shift_reg shift_reg_4 (.SCLK(and_1_out), .SIN(SI), .EN(decoder_1_out_3), .Q(shift_reg_4_q));  // open: OF
  Comparator #(.Bits(8)) comparator_1 (.a({clks_out, \byte , \bit }), .b(8'h20), .eq(comparator_1_eq));  // open: gt, lt
  Sub #(.Bits(3)) sub_1 (.a(3'b111), .b(counter_1_out[2:0]), .c_i(1'b0), .s(sub_1_s));  // open: c_o
  not not_2 (not_2_out, and_1_out);
  Comparator #(.Bits(3)) comparator_2 (.a(\byte ), .b(3'b100), .lt(comparator_2_lt));  // open: gt, eq
  // Probe opcode on shift_reg_1_q
  // Probe a2 on shift_reg_2_q
  // Probe a1 on shift_reg_3_q
  // Probe a0 on shift_reg_4_q
  and and_2 (and_2_out, comparator_1_eq, not_2_out);
  Register #(.Bits(20)) register_1 (
    .D({shift_reg_2_q[3:0], shift_reg_3_q, shift_reg_4_q[6:0], SI}), .C(and_1_out), .en(comparator_2_lt),
    .Q(register_1_q));
  D_FF_AS d_ff_as_1 (.Set(1'b0), .D(1'b1), .C(and_2_out), .Clr(CE), .Q(d_ff_as_1_q));  // open: nQ
  Add #(.Bits(20)) add_1 (.a(counter_1_out[22:3]), .b(register_1_q), .c_i(1'b0), .s(add_1_s));  // open: c_o
  // Probe on {shift_reg_2_q[3:0], shift_reg_3_q, shift_reg_4_q[6:0], SI}
  // Probe addr on add_1_s
  ROM #(.AddrBits(20), .Bits(8)) rom_1 (.A(add_1_s), .sel(1'b1), .D(rom_1_d));
  BitSelector #(.Selector_Bits(3)) bitselector_1 (.in(rom_1_d), .sel(sub_1_s), .out(bitselector_1_out));
  // Probe data on rom_1_d
  assign SO = d_ff_as_1_q ? bitselector_1_out : 1'bz;  // Driver driver_1

  // Notes on the sheet:
  //   CE: default 1
  //   HOLD: default 1
  //   contents of rom_1 (hex, n*v repeats v):
  //   74582*0,96,69887*0,96,5a
endmodule

/* Test case opcode:
          CE_ SCLK opcode SI                    a2   a1   a0   addr     data SO
          1   0    x      x                     x    x    x    x        0    x
repeat(8) 0   C    X      ((0x03 >> (7-n))&0x1) X    X    x    X        0    X
repeat(8) 0   C    0x3    ((0x12 >> (7-n))&0x1) X    X    x    X        0    X
repeat(8) 0   C    0x3    ((0x34 >> (7-n))&0x1) 0x12 X    x    X        0    X
repeat(8) 0   C    0x3    ((0x56 >> (7-n))&0x1) 0x12 0x34 x    X        X    X          
loop(n,8)
          0   0    0x3    0                     0x12 0x34 0x56 0x23456 0x96 ((0x96 >> (7-n)&0x1))   
          0   1    0x3    0                     0x12 0x34 0x56 0x23456 0x96 ((0x96 >> (7-n)&0x1))   
end loop
loop(n,8)
          0   0    0x3    0                     0x12 0x34 0x56 0x23457 0x5A ((0x5A >> (7-n)&0x1))   
          0   1    0x3    0                     0x12 0x34 0x56 0x23457 0x5A ((0x5A >> (7-n)&0x1))   
end loop
*/
