// Digital circuit shift_reg.dig as structural Verilog
module shift_reg (
  input  SCLK,
  input  SIN,
  input  EN,
  input  RST,
  output [7:0] Q,
  output OF
);

  wire and_1_out;

  and and_1 (and_1_out, SCLK, EN);
  CounterPreset #(.Bits(8)) counterpreset_1 (
    .en(1'b1), .C(and_1_out), .dir(1'b0), .in({Q[6:0], SIN}), .ld(1'b1), .clr(RST), .out(Q));  // open: ovf
  D_FF d_ff_1 (.D(Q[7]), .C(and_1_out), .Q(OF));  // open: nQ
endmodule

/* Test case 8 bits:
SIN SCLK Q    OF RST_ EN
1   C    X    X  0    1
0   C    X    X  0    1
1   C    X    X  0    1
0   C    X    X  0    1
0   C    X    X  0    1
1   C    X    X  0    1
1   C    X    X  0    1
0   C    0xa6 X  0    1
0   C    X    1  0    1
0   C    X    0  0    1
*/
