// Digital circuit spicomp.dig as structural Verilog
module spicomp (
  input  RST,
  input  CLK
);

  wire and_1_out, bitselector_1_out, comparator_1_eq, comparator_2_eq, decoder_1_out_0, decoder_1_out_1,
       decoder_1_out_6, IR_NEXT_pin18, not_1_out, not_2_out, not_3_out, not_4_out, notconnected_3_out,
       notconnected_4_out, notconnected_5_out, notconnected_6_out, ROM_so, X_pin11, X_pin17, X_pin18;
  wire [5:0] counter_1_out;
  wire [7:0] _74273_1_pin2, IR_NEXT_pin4, multiplexer_2_out, multiplexer_3_out, notconnected_7_out,
       notconnected_8_out, notconnected_9_out, PROG_q;
  wire [19:0] ROM_rom_addr;

  not not_1 (not_1_out, CLK);
  not not_2 (not_2_out, RST);
  Counter #(.Bits(6)) counter_1 (.en(1'b1), .C(CLK), .clr(not_2_out), .out(counter_1_out));  // open: ovf
  // Probe bit on counter_1_out[2:0]
  // Probe byte on counter_1_out[5:3]
  // Probe on multiplexer_3_out[2:0]
  Decoder #(.Selector_Bits(3)) decoder_1 (
    .sel(multiplexer_3_out[2:0]), .out_0(decoder_1_out_0), .out_1(decoder_1_out_1), .out_6(decoder_1_out_6));  // open: out_2, out_3, out_4, out_5, out_7
  // Probe on multiplexer_3_out[6:4]
  not not_3 (not_3_out, decoder_1_out_0);
  serial_rom ROM (
    .SCLK(not_1_out), .SI(X_pin11), .CE(multiplexer_3_out[3]), .HOLD(not_3_out), .TEST(1'b1), .ROM_D(PROG_q),
    .SO(ROM_so), .ROM_ADDR(ROM_rom_addr));  // open: bit, byte
  RAMAsync #(.AddrBits(20), .Bits(8)) PROG (.A(ROM_rom_addr), .D({8{1'b0}}), .we(1'b0), .Q(PROG_q));
  _74299 X (
    .pin1(decoder_1_out_1), .pin2(1'b0), .pin3(1'b0), .pin9(RST), .pin10(1'b0), .pin11(X_pin11),
    .pin12(not_1_out), .pin17(X_pin17), .pin18(X_pin18), .pin19(1'b0), .pin20(1'b1));  // open: pin4, pin5, pin6, pin7, pin8, pin13, pin14, pin15, pin16
  _74299 IR_NEXT (
    .pin1(decoder_1_out_6), .pin2(1'b0), .pin3(1'b0), .pin4(IR_NEXT_pin4[6]), .pin5(IR_NEXT_pin4[4]),
    .pin6(IR_NEXT_pin4[2]), .pin7(IR_NEXT_pin4[0]), .pin9(RST), .pin10(1'b0), .pin11(X_pin11),
    .pin12(not_1_out), .pin13(IR_NEXT_pin4[1]), .pin14(IR_NEXT_pin4[3]), .pin15(IR_NEXT_pin4[5]),
    .pin16(IR_NEXT_pin4[7]), .pin18(IR_NEXT_pin18), .pin19(1'b0), .pin20(1'b1));  // open: pin8, pin17
  // NotConnected on X_pin18
  // NotConnected on IR_NEXT_pin18
  // Probe PROG_DATA on PROG_q
  // Probe PROG_ADDR on ROM_rom_addr
  BitSelector #(.Selector_Bits(3)) bitselector_1 (.in(8'hc0), .sel(counter_1_out[2:0]), .out(bitselector_1_out));
  // NotConnected on notconnected_3_out
  // NotConnected on notconnected_4_out
  // NotConnected on notconnected_5_out
  // NotConnected on notconnected_6_out
  // Probe IR_SR on IR_NEXT_pin4
  Multiplexer #(.Selector_Bits(3)) multiplexer_1 (
    .sel(multiplexer_3_out[6:4]), .in_0(ROM_so), .in_1(X_pin17), .in_2(X_pin17), .in_3(X_pin17),
    .in_4(notconnected_3_out), .in_5(notconnected_4_out), .in_6(notconnected_5_out),
    .in_7(bitselector_1_out), .out(X_pin11));
  Comparator #(.Bits(3)) comparator_1 (.a(counter_1_out[2:0]), .b(3'b111), .eq(comparator_1_eq));  // open: gt, lt
  and and_1 (and_1_out, comparator_1_eq, not_4_out, decoder_1_out_6);
  not not_4 (not_4_out, not_1_out);
  // Probe SER_BUS on X_pin11
  _74273 _74273_1 (
    .pin1(RST), .pin2(_74273_1_pin2[0]), .pin3(IR_NEXT_pin4[0]), .pin4(IR_NEXT_pin4[1]),
    .pin5(_74273_1_pin2[1]), .pin6(_74273_1_pin2[2]), .pin7(IR_NEXT_pin4[2]), .pin8(IR_NEXT_pin4[3]),
    .pin9(_74273_1_pin2[3]), .pin10(1'b0), .pin11(and_1_out), .pin12(_74273_1_pin2[4]),
    .pin13(IR_NEXT_pin4[4]), .pin14(IR_NEXT_pin4[5]), .pin15(_74273_1_pin2[5]), .pin16(_74273_1_pin2[6]),
    .pin17(IR_NEXT_pin4[6]), .pin18(IR_NEXT_pin4[7]), .pin19(_74273_1_pin2[7]), .pin20(1'b1));
  // NotConnected on notconnected_7_out
  // NotConnected on notconnected_8_out
  // NotConnected on notconnected_9_out
  Multiplexer #(.Selector_Bits(3), .Bits(8)) multiplexer_2 (
    .sel(counter_1_out[5:3]), .in_0(8'h78), .in_1(8'h60), .in_2(8'h10), .in_3(8'h20), .in_4(8'h30),
    .in_5(8'h6), .in_6(notconnected_7_out), .in_7(notconnected_8_out), .out(multiplexer_2_out));
  Comparator #(.Bits(8)) comparator_2 (.a({8{1'b0}}), .b(_74273_1_pin2), .eq(comparator_2_eq));  // open: gt, lt
  Multiplexer #(.Bits(8)) multiplexer_3 (
    .sel(comparator_2_eq), .in_0(_74273_1_pin2), .in_1(multiplexer_2_out), .out(multiplexer_3_out));
  // Probe IR on _74273_1_pin2
  // Probe IR_eff on multiplexer_3_out
endmodule

/* Test case boot:
           RST_ CLK IR
	   0    0   0
loop(n,32)
           1    0   X
           1    1   X
end loop
loop(n,8)
           1    0   X
           1    1   X
end loop
           1    0   0xAB
loop(n,7)
           1    C   0xAB
end loop
           1    0   0xAB
           1    1   0xAB
           1    0   0xCD
memory PROG(0x0)=0xAB;
memory PROG(0x1)=0xCD;
*/
