// Digital circuit lutcomp.dig as structural Verilog
module lutcomp (
  input  RESET,
  input  clk,
  output HALT
);

  wire CLK_t, CLK_t_t, nor_1_out, not_2_out, not_3_out, rs_ff_as_1_nq, rs_ff_as_1_q, switch_1_b, switch_2_b,
       switch_3_b, uc_1_a0_cp, uc_1_a1_cp, uc_1_a2_cp, uc_1_addr_oe, uc_1_alu_cp, uc_1_alu_oe, uc_1_in1_cp,
       uc_1_mem_cp, uc_1_mem_oe, uc_1_pc_inc, uc_1_pc_spe, uc_1_ttyin_cp, uc_1_ttyin_oe, uc_1_ttyout_cp,
       uc_1_w_cp, uc_1_w_oe, uc_1_x_cp, uc_1_x_oe, uc_1_y_cp, uc_1_y_oe, uc_1_z_cp, uc_1_z_oe;
  wire [1:0] uc_1_stage;
  wire [2:0] uc_1_alu_op;
  wire [3:0] uc_1_uaddr_3;
  wire [6:0] keyboard_1_d, uc_1_uaddr;
  wire [7:0] multiplexer_1_out, telnet_1_out, uc_1_data, uc_1_uaddr_2, uc_1_udata, uc_1_uir0, uc_1_uir1,
       uc_1_upc;
  wire [7:7] keyboard_1_av, telnet_1_av;
  wire [15:7] keyboard_1_d_2;
  wire [23:0] pc_1_pc, undriven;

  and and_1 (CLK_t, clk, HALT);
  Stop stop_1 (.stop(~HALT));
  not not_1 (CLK_t_t, CLK_t);
  uc uc_1 (
    .CLK(CLK_t_t), .RESET(RESET), .DATA(uc_1_data), .ADDR_OE(uc_1_addr_oe), .ALU_OP(uc_1_alu_op),
    .PC_INC(uc_1_pc_inc), .IN1_CP(uc_1_in1_cp), .ALU_CP(uc_1_alu_cp), .MEM_CP(uc_1_mem_cp),
    .TTYIN_CP(uc_1_ttyin_cp), .W_CP(uc_1_w_cp), .X_CP(uc_1_x_cp), .Y_CP(uc_1_y_cp), .Z_CP(uc_1_z_cp),
    .A0_CP(uc_1_a0_cp), .A1_CP(uc_1_a1_cp), .A2_CP(uc_1_a2_cp), .TTYOUT_CP(uc_1_ttyout_cp), .HALT(HALT),
    .ALU_OE(uc_1_alu_oe), .MEM_OE(uc_1_mem_oe), .TTYIN_OE(uc_1_ttyin_oe), .PC_SPE(uc_1_pc_spe),
    .W_OE(uc_1_w_oe), .X_OE(uc_1_x_oe), .Y_OE(uc_1_y_oe), .Z_OE(uc_1_z_oe), .uIR0(uc_1_uir0),
    .uIR1(uc_1_uir1), .uAddr({uc_1_uaddr_3, uc_1_uaddr_2, uc_1_uaddr}), .uPC(uc_1_upc), .stage(uc_1_stage),
    .uData(uc_1_udata));
  not not_2 (not_2_out, uc_1_addr_oe);
  // Probe on uc_1_uir0
  // Probe on uc_1_uir1
  // Probe on uc_1_upc
  // Probe on uc_1_stage
  // Probe on uc_1_udata
  Switch switch_1 (.A(uc_1_pc_inc), .B(switch_1_b));
  pc pc_1 (.PC_INC(uc_1_pc_inc), .RESET(RESET), .PC_SPE(uc_1_pc_spe), .OE(not_2_out), .ADDR(undriven), .PC(pc_1_pc));
  // Probe $uPC on {uc_1_uaddr_3, uc_1_uaddr_2, uc_1_uaddr}
  // Probe on uc_1_uaddr
  // Probe $IR0 on uc_1_uaddr_2
  // Probe $FLAGS on uc_1_uaddr_3
  Break break_1 (.brk(switch_1_b));
  PullDown pulldown_1 (.out(switch_1_b));
  RS_FF_AS rs_ff_as_1 (.S(uc_1_ttyout_cp), .R(uc_1_ttyin_cp), .Q(rs_ff_as_1_q), .nQ(rs_ff_as_1_nq));
  nor nor_1 (nor_1_out, uc_1_ttyout_cp, uc_1_ttyin_cp);
  Keyboard keyboard_1 (.C(uc_1_ttyin_cp), .en(1'b1), .D({keyboard_1_d_2, keyboard_1_d}), .av(keyboard_1_av[7]));
  // Probe PC on pc_1_pc
  Terminal terminal_1 (.D(uc_1_data), .C(uc_1_ttyout_cp), .en(1'b1));
  Switch switch_2 (.A(uc_1_ttyin_cp), .B(switch_2_b));
  Telnet #(.telnetEscape("false"), .port(45454)) telnet_1 (
    .in(uc_1_data), .C(nor_1_out), .wr(rs_ff_as_1_q), .rd(rs_ff_as_1_nq), .out(telnet_1_out),
    .av(telnet_1_av[7]));
  Multiplexer #(.Bits(8)) multiplexer_1 (
    .sel(keyboard_1_av[7]), .in_0({telnet_1_av[7], telnet_1_out[6:0]}),
    .in_1({keyboard_1_av[7], keyboard_1_d}), .out(multiplexer_1_out));
  Break break_2 (.brk(switch_2_b));
  PullDown pulldown_2 (.out(switch_2_b));
  memory memory_1 (
    .MEM_CP(uc_1_mem_cp), .ADDR_OE(uc_1_addr_oe), .A0_CP(uc_1_a0_cp), .A1_CP(uc_1_a1_cp), .A2_CP(uc_1_a2_cp),
    .MEM_OE(uc_1_mem_oe), .DATA(uc_1_data), .ADDR(undriven));
  \reg  W (.OE(uc_1_w_oe), .CP(uc_1_w_cp), .DATA(uc_1_data));  // open: IO
  \reg  X (.OE(uc_1_x_oe), .CP(uc_1_x_cp), .DATA(uc_1_data));  // open: IO
  \reg  Y (.OE(uc_1_y_oe), .CP(uc_1_y_cp), .DATA(uc_1_data));  // open: IO
  \reg  Z (.OE(uc_1_z_oe), .CP(uc_1_z_cp), .DATA(uc_1_data));  // open: IO
  assign uc_1_data = ~uc_1_ttyin_oe ? multiplexer_1_out : 8'bz;  // DriverInvSel driverinvsel_1
  not not_3 (not_3_out, uc_1_ttyin_oe);
  // Probe ADDR on undriven
  // Probe DATA on uc_1_data
  Switch switch_3 (.A(not_3_out), .B(switch_3_b));
  PullDown pulldown_3 (.out(switch_3_b));
  Break break_3 (.brk(switch_3_b));
  alu alu_1 (
    .ALU_OP(uc_1_alu_op), .ALU_OE(uc_1_alu_oe), .ALU_CP(uc_1_alu_cp), .IN1_CP(uc_1_in1_cp), .DATA(uc_1_data));  // open: IN1, ALU_REG, ALU_RESULT

  // Notes on the sheet:
  //   RESET: default 1
  //   clk: Hz: 1000000
  //   4A
  //   4B
  //   4Y
  //   6A
  //   6Y
  //   3A
  //   3Y
endmodule

/* Test case:
RESET_ HALT
0      1
*/
