// Digital circuit memory.dig as structural Verilog
module memory (
  input  MEM_CP,
  input  ADDR_OE,
  input  A0_CP,
  input  A1_CP,
  input  A2_CP,
  input  MEM_OE,
  input  [7:0] DATA_2,
  input  DATA_OE,
  output [7:0] DATA,
  output [23:0] ADDR
);

  wire not_1_out, not_2_out, not_3_out, or_1_out;
  wire [7:0] ROM_d;

  PullDown pulldown_1 (.out(DATA_OE));
  PullDown #(.Bits(8)) pulldown_2 (.out(DATA_2));
  assign DATA = DATA_OE ? DATA_2 : 8'bz;  // Driver driver_1
  // _74574 ADDR0: pin names not known; wires that end beside it: ADDR_OE, 1'b1
  // _74574 ADDR1: pin names not known; wires that end beside it: 1'b0, ADDR_OE, A0_CP, 1'b1
  // _74574 ADDR2: pin names not known; wires that end beside it: 1'b0, ADDR_OE, 1'b0, A1_CP, 1'b1, A2_CP
  not not_1 (not_1_out, MEM_CP);
  not not_2 (not_2_out, ADDR[19]);
  not not_3 (not_3_out, ADDR[19]);
  RAM ram_1 (.CE(not_2_out), .OE(MEM_OE), .WE(not_1_out), .A(ADDR[18:0]), .D(DATA));
  or or_1 (or_1_out, MEM_OE, ADDR[19]);
  ROM #(.AddrBits(19), .Bits(8)) ROM (.A(ADDR[18:0]), .sel(not_3_out), .D(ROM_d));
  assign DATA = ~or_1_out ? ROM_d : 8'bz;  // DriverInvSel driverinvsel_1

  // Notes on the sheet:
  //   5A
  //   5Y
  //   6A
  //   6Y
  //   ROM
  //   ROM loads echo.j.hex
endmodule

/* Test case:
ADDR_OE_ MEM_OE_ $DATA $DATA_OE  A0_CP A1_CP A2_CP MEM_CP DATA
0        1       0x00  1         C     0     0     0      0x00
0        1       0x00  1         0     C     0     0      0x00
0        1       0x00  1         0     0     C     0      0x00
0        0       Z     0         0     0     0     0      0x0F
0        1       0x08  1         0     0     C     0      0x08
0        1       0xAA  1         0     0     0     C      0xAA
0        1       0x01  1         C     0     0     0      0x01
0        1       0xBB  1         0     0     0     C      0xBB
0        1       0x00  1         C     0     0     0      0x00
0        0       Z     0         0     0     0     0      0xAA
0        1       0x01  1         C     0     0     0      0x01
0        0       Z     0         0     0     0     0      0xBB
*/
