// Digital circuit pc.dig as structural Verilog
module pc (
  input  PC_INC,
  input  RESET,
  input  PC_SPE,
  input  OE,
  input  [23:0] ADDR,
  output [23:0] PC
);

  wire PC0_pin15, PC1_pin15, PC2_pin15, PC3_pin15, PC4_pin15;

  _74161 PC0 (
    .pin1(RESET), .pin2(PC_INC), .pin3(ADDR[0]), .pin4(ADDR[1]), .pin5(ADDR[2]), .pin6(ADDR[3]), .pin7(1'b1),
    .pin8(1'b0), .pin9(PC_SPE), .pin10(1'b1), .pin11(PC[3]), .pin12(PC[2]), .pin13(PC[1]), .pin14(PC[0]),
    .pin15(PC0_pin15), .pin16(1'b1));
  _74161 PC1 (
    .pin1(RESET), .pin2(PC_INC), .pin3(ADDR[4]), .pin4(ADDR[5]), .pin5(ADDR[6]), .pin6(ADDR[7]),
    .pin7(PC0_pin15), .pin8(1'b0), .pin9(PC_SPE), .pin10(1'b1), .pin11(PC[7]), .pin12(PC[6]), .pin13(PC[5]),
    .pin14(PC[4]), .pin15(PC1_pin15), .pin16(1'b1));
  _74161 PC2 (
    .pin1(RESET), .pin2(PC_INC), .pin3(ADDR[8]), .pin4(ADDR[9]), .pin5(ADDR[10]), .pin6(ADDR[11]),
    .pin7(PC0_pin15), .pin8(1'b0), .pin9(PC_SPE), .pin10(PC1_pin15), .pin11(PC[11]), .pin12(PC[10]),
    .pin13(PC[9]), .pin14(PC[8]), .pin15(PC2_pin15), .pin16(1'b1));
  _74161 PC3 (
    .pin1(RESET), .pin2(PC_INC), .pin3(ADDR[12]), .pin4(ADDR[13]), .pin5(ADDR[14]), .pin6(ADDR[15]),
    .pin7(PC0_pin15), .pin8(1'b0), .pin9(PC_SPE), .pin10(PC2_pin15), .pin11(PC[15]), .pin12(PC[14]),
    .pin13(PC[13]), .pin14(PC[12]), .pin15(PC3_pin15), .pin16(1'b1));
  _74161 PC4 (
    .pin1(RESET), .pin2(PC_INC), .pin3(ADDR[16]), .pin4(ADDR[17]), .pin5(ADDR[18]), .pin6(ADDR[19]),
    .pin7(PC0_pin15), .pin8(1'b0), .pin9(PC_SPE), .pin10(PC3_pin15), .pin11(PC[19]), .pin12(PC[18]),
    .pin13(PC[17]), .pin14(PC[16]), .pin15(PC4_pin15), .pin16(1'b1));
  _74161 PC5 (
    .pin1(RESET), .pin2(PC_INC), .pin3(ADDR[20]), .pin4(ADDR[21]), .pin5(ADDR[22]), .pin6(ADDR[23]),
    .pin7(PC0_pin15), .pin8(1'b0), .pin9(PC_SPE), .pin10(PC4_pin15), .pin11(PC[23]), .pin12(PC[22]),
    .pin13(PC[21]), .pin14(PC[20]), .pin16(1'b1));  // open: pin15
  assign ADDR = ~OE ? PC : 24'bz;  // DriverInvSel driverinvsel_1
endmodule

/* Test case pc:
OE_ PC_SPE_ PC_INC RESET_ ADDR ADDR_out
X X X 0 Z X
0 1 0 1 Z 0
repeat(256) 0 1 C 1 Z (n+1)
loop (i, 7)
	1 0 C 1 ((1<<(4*i))-1) ((1<<(4*i))-1)
	0 1 0 1 Z ((1<<(4*i))-1)
	0 1 C 1 Z ((1<<(4*i))+0)
	0 1 C 1 Z ((1<<(4*i))+1)
end loop
*/
