// Digital circuit reg.dig as structural Verilog
module \reg  (
  input  [7:0] IO,
  input  OE,
  input  CP
);

  _74299 _74299_1 (
    .pin1(OE), .pin2(OE), .pin3(OE), .pin4(IO[6]), .pin5(IO[4]), .pin6(IO[2]), .pin7(IO[0]), .pin9(1'b1),
    .pin10(1'b0), .pin11(1'b0), .pin12(CP), .pin13(IO[1]), .pin14(IO[3]), .pin15(IO[5]), .pin16(IO[7]),
    .pin18(1'b0), .pin19(OE), .pin20(1'b1));  // open: pin8, pin17
endmodule
