// Logisim project lutcomp.circ as structural Verilog: 1 circuit, main circuit main
// 10
module main (
);

  wire and_1_out, and_2_out, clock_1_out, comparator_1_eq, decoder_1_out0, decoder_1_out1, decoder_1_out2,
       decoder_1_out3, decoder_1_out4, decoder_2_out0, decoder_2_out1, decoder_2_out2, decoder_2_out3,
       decoder_3_out0, decoder_3_out1, decoder_3_out2, decoder_3_out3, not_1_out, not_2_out, or_1_out,
       or_2_out;
  wire [1:0] rom_1_data_2;
  wire [2:0] counter_1_q;
  wire [7:0] adder_1_out, ADDR_q, controlled_buffer_5_out, multiplexer_1_out, PC_q, register_1_q;
  wire [13:0] rom_1_data;
  wire [15:0] rom_2_data;
  wire [19:0] ACC_q;

  Clock clock_1 (.out(clock_1_out));
  Counter #(.width(3), .max('h4)) counter_1 (.Q(counter_1_q), .clk(clock_1_out));  // open: load, D, count, carry, clr
  Adder adder_1 (.a(PC_q), .b(8'h1), .out(adder_1_out));  // open: cin, cout
  Decoder #(.select(3), .disabled(0)) decoder_1 (
    .out0(decoder_1_out0), .out1(decoder_1_out1), .out2(decoder_1_out2), .out3(decoder_1_out3),
    .out4(decoder_1_out4), .sel(counter_1_q), .en(not_1_out));  // open: out5, out6, out7
  Multiplexer #(.width(8), .enable("false")) multiplexer_1 (
    .in0(adder_1_out), .in1(rom_2_data[7:0]), .out(multiplexer_1_out), .sel(decoder_3_out2));
  Register register_1 (.D(multiplexer_1_out), .Q(register_1_q), .clk(decoder_1_out3));  // open: en, clr
  Register PC (.D(register_1_q), .Q(PC_q), .clk(decoder_1_out4));  // open: en, clr
  Register ACC (.D(rom_2_data[7:0]), .en(decoder_3_out0), .Q(ACC_q[7:0]), .clk(decoder_1_out3));  // open: clr
  not not_1 (not_1_out, rom_2_data[15]);
  // Probe on rom_1_data_2
  ROM #(.dataWidth(16)) rom_1 (
    .addr(PC_q), .data({rom_1_data_2, rom_1_data[13:12], ACC_q[19:16], rom_1_data[7:0]}));  // open: sel
  // Probe on rom_1_data[7:0]
  assign ACC_q[15:8] = decoder_2_out0 ? rom_1_data[7:0] : 8'bz;  // Controlled_Buffer controlled_buffer_1
  Decoder #(.select(2), .disabled(0), .enable("false")) decoder_2 (
    .out0(decoder_2_out0), .out1(decoder_2_out1), .out2(decoder_2_out2), .out3(decoder_2_out3),
    .sel(rom_1_data_2));
  // Probe on ACC_q[19:16]
  assign ACC_q[15:8] = decoder_2_out1 ? ADDR_q : 8'bz;  // Controlled_Buffer controlled_buffer_2
  assign ACC_q[15:8] = decoder_2_out2 ? PC_q : 8'bz;  // Controlled_Buffer controlled_buffer_3
  Register ADDR (.D(rom_2_data[7:0]), .en(decoder_3_out1), .Q(ADDR_q), .clk(decoder_1_out3));  // open: clr
  Comparator comparator_1 (.a({8{1'b0}}), .b(ADDR_q), .eq(comparator_1_eq));  // open: gt, lt
  assign ACC_q[15:8] = decoder_2_out3 ? controlled_buffer_5_out : 8'bz;  // Controlled_Buffer controlled_buffer_4
  and and_1 (and_1_out, comparator_1_eq, and_2_out);
  TTY tty_1 (.data(rom_2_data[6:0]), .clk(decoder_1_out3), .we(and_1_out));  // open: clr
  // Probe on ACC_q[15:8]
  assign controlled_buffer_5_out = and_2_out ? rom_2_data[7:0] : 8'bz;  // Controlled_Buffer controlled_buffer_5
  not not_2 (not_2_out, and_2_out);
  and and_2 (and_2_out, or_1_out, decoder_3_out3);
  or or_1 (or_1_out, decoder_1_out2, decoder_1_out3);
  or or_2 (or_2_out, decoder_1_out3, decoder_1_out1);
  // Probe on ACC_q[7:0]
  RAM ram_1 (.addr(ADDR_q), .data(controlled_buffer_5_out), .clk(or_2_out), .ld(not_2_out));  // open: sel, clr
  ROM #(.addrWidth(20), .dataWidth(16)) rom_2 (.addr(ACC_q), .data(rom_2_data));  // open: sel
  // Probe on rom_2_data[7:0]
  // Probe on controlled_buffer_5_out
  Decoder #(.select(2), .disabled(0), .enable("false")) decoder_3 (
    .out0(decoder_3_out0), .out1(decoder_3_out1), .out2(decoder_3_out2), .out3(decoder_3_out3),
    .sel(rom_1_data[13:12]));

  // Notes on the sheet:
  //   instructions
  //   contents of rom_1 (hex, n*v repeats v):
  //   1001 30ff 1000 3048 3069 3021 300d 1002 3003 1002 c0ff 230 1000 31ff 1002 c0ff 2ff 31ff a3ff f5 a2ff
  //   ffff
  //   ALU LUT
  //   contents of rom_2 (hex, n*v repeats v):
  //   256*0 256*1 256*2 256*3 256*4 256*5 256*6 256*7 256*8 256*9 256*a 256*b 256*c 256*d 256*e 256*f
  //   256*10 256*11 256*12 256*13 256*14 256*15 256*16 256*17 256*18 256*19 256*1a 256*1b 256*1c 256*1d
  //   256*1e 256*1f 256*20 256*21 256*22 256*23 256*24 256*25 256*26 256*27 256*28 256*29 256*2a 256*2b
  //   256*2c 256*2d 256*2e 256*2f 256*30 256*31 256*32 256*33 256*34 256*35 256*36 256*37 256*38 256*39
  //   256*3a 256*3b 256*3c 256*3d 256*3e 256*3f 256*40 256*41 256*42 256*43 256*44 256*45 256*46 256*47
  //   256*48 256*49 256*4a 256*4b 256*4c 256*4d 256*4e 256*4f 256*50 256*51 256*52 256*53 256*54 256*55
  //   256*56 256*57 256*58 256*59 256*5a 256*5b 256*5c 256*5d 256*5e 256*5f 256*60 256*61 256*62 256*63
  //   256*64 256*65 256*66 256*67 256*68 256*69 256*6a 256*6b 256*6c 256*6d 256*6e 256*6f 256*70 256*71
  //   256*72 256*73 256*74 256*75 256*76 256*77 256*78 256*79 256*7a 256*7b 256*7c 256*7d 256*7e 256*7f
  //   256*80 256*81 256*82 256*83 256*84 256*85 256*86 256*87 256*88 256*89 256*8a 256*8b 256*8c 256*8d
  //   256*8e 256*8f 256*90 256*91 256*92 256*93 256*94 256*95 256*96 256*97 256*98 256*99 256*9a 256*9b
  //   256*9c 256*9d 256*9e 256*9f 256*a0 256*a1 256*a2 256*a3 256*a4 256*a5 256*a6 256*a7 256*a8 256*a9
  //   256*aa 256*ab 256*ac 256*ad 256*ae 256*af 256*b0 256*b1 256*b2 256*b3 256*b4 256*b5 256*b6 256*b7
  //   256*b8 256*b9 256*ba 256*bb 256*bc 256*bd 256*be 256*bf 256*c0 256*c1 256*c2 256*c3 256*c4 256*c5
  //   256*c6 256*c7 256*c8 256*c9 256*ca 256*cb 256*cc 256*cd 256*ce 256*cf 256*d0 256*d1 256*d2 256*d3
  //   256*d4 256*d5 256*d6 256*d7 256*d8 256*d9 256*da 256*db 256*dc 256*dd 256*de 256*df 256*e0 256*e1
  //   256*e2 256*e3 256*e4 256*e5 256*e6 256*e7 256*e8 256*e9 256*ea 256*eb 256*ec 256*ed 256*ee 256*ef
  //   256*f0 256*f1 256*f2 256*f3 256*f4 256*f5 256*f6 256*f7 256*f8 256*f9 256*fa 256*fb 256*fc 256*fd
  //   256*fe 256*ff 0 1 2 3 4 5 6 7 8 9 a b c d e f 10 11 12 13 14 15 16 17 18 19 1a 1b 1c 1d 1e 1f 20 21
  //   22 23 24 25 26 27 28 29 2a 2b 2c 2d 2e 2f 30 31 32 33 34 35 36 37 38 39 3a 3b 3c 3d 3e 3f 40 41 42
  //   43 44 45 46 47 48 49 4a 4b 4c 4d 4e 4f 50 51 52 53 54 55 56 57 58 59 5a 5b 5c 5d 5e 5f 60 61 62 63
  //   64 65 66 67 68 69 6a 6b 6c 6d 6e 6f 70 71 72 73 74 75 76 77 78 79 7a 7b 7c 7d 7e 7f 80 81 82 83 84
  //   85 86 87 88 89 8a 8b 8c 8d 8e 8f 90 91 92 93 94 95 96 97 98 99 9a 9b 9c 9d 9e 9f a0 a1 a2 a3 a4 a5
  //   a6 a7 a8 a9 aa ab ac ad ae af b0 b1 b2 b3 b4 b5 b6 b7 b8 b9 ba bb bc bd be bf c0 c1 c2 c3 c4 c5 c6
  //   c7 c8 c9 ca cb cc cd ce cf d0 d1 d2 d3 d4 d5 d6 d7 d8 d9 da db dc dd de df e0 e1 e2 e3 e4 e5 e6 e7
  //   e8 e9 ea eb ec ed ee ef f0 f1 f2 f3 f4 f5 f6 f7 f8 f9 fa fb fc fd fe ff 0 1 2 3 4 5 6 7 8 9 a b c d
  //   e f 10 11 12 13 14 15 16 17 18 19 1a 1b 1c 1d 1e 1f 20 21 22 23 24 25 26 27 28 29 2a 2b 2c 2d 2e 2f
  //   30 31 32 33 34 35 36 37 38 39 3a 3b 3c 3d 3e 3f 40 41 42 43 44 45 46 47 48 49 4a 4b 4c 4d 4e 4f 50
  //   51 52 53 54 55 56 57 58 59 5a 5b 5c 5d 5e 5f 60 61 62 63 64 65 66 67 68 69 6a 6b 6c 6d 6e 6f 70 71
  //   72 73 74 75 76 77 78 79 7a 7b 7c 7d 7e 7f 80 81 82 83 84 85 86 87 88 89 8a 8b 8c 8d 8e 8f 90 91 92
  //   93 94 95 96 97 98 99 9a 9b 9c 9d 9e 9f a0 a1 a2 a3 a4 a5 a6 a7 a8 a9 aa ab ac ad ae af b0 b1 b2 b3
  //   b4 b5 b6 b7 b8 b9 ba bb bc bd be bf c0 c1 c2 c3 c4 c5 c6 c7 c8 c9 ca cb cc cd ce cf d0 d1 d2 d3 d4
  //   d5 d6 d7 d8 d9 da db dc dd de df e0 e1 e2 e3 e4 e5 e6 e7 e8 e9 ea eb ec ed ee ef f0 f1 f2 f3 f4 f5
  //   f6 f7 f8 f9 fa fb fc fd fe ff 0 1 2 3 4 5 6 7 8 9 a b c d e f 10 11 12 13 14 15 16 17 18 19 1a 1b 1c
  //   1d 1e 1f 20 21 22 23 24 25 26 27 28 29 2a 2b 2c 2d 2e 2f 30 31 32 33 34 35 36 37 38 39 3a 3b 3c 3d
  //   3e 3f 40 41 42 43 44 45 46 47 48 49 4a 4b 4c 4d 4e 4f 50 51 52 53 54 55 56 57 58 59 5a 5b 5c 5d 5e
  //   5f 60 61 62 63 64 65 66 67 68 69 6a 6b 6c 6d 6e 6f 70 71 72 73 74 75 76 77 78 79 7a 7b 7c 7d 7e 7f
  //   80 81 82 83 84 85 86 87 88 89 8a 8b 8c 8d 8e 8f 90 91 92 93 94 95 96 97 98 99 9a 9b 9c 9d 9e 9f a0
  //   a1 a2 a3 a4 a5 a6 a7 a8 a9 aa ab ac ad ae af b0 b1 b2 b3 b4 b5 b6 b7 b8 b9 ba bb bc bd be bf c0 c1
  //   c2 c3 c4 c5 c6 c7 c8 c9 ca cb cc cd ce cf d0 d1 d2 d3 d4 d5 d6 d7 d8 d9 da db dc dd de df e0 e1 e2
  //   e3 e4 e5 e6 e7 e8 e9 ea eb ec ed ee ef f0 f1 f2 f3 f4 f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
endmodule
